// Logisim project TinyCPU-8-8.circ as structural Verilog: 29 circuits, main circuit TinyCPUMain
module TinyCPUMain (
  input  CLK,
  input  RESET,
  output [15:0] PRINT_VALUE,
  output PRINT_ADDRESS_VALID,
  output [5:0] PRINT_ADDRESS_VALUE,
  output PRINT_VALID,
  output ERROR_OVF,
  output ERROR_DIV0,
  output ERROR_ADDR,
  output ERROR_INV,
  output ERROR_ILL,
  output ERROR_INPUT,
  output PRINT_ENABLE,
  output PRINT_ADDRESS_ENABLE,
  output HALTED,
  output HALTED_WITH_ERROR
);

  wire ADDRESS_PATH_p2, ADDRESS_PATH_p7, ADDRESS_PATH_p8, ADDRESS_PATH_p9, ADDRESS_PATH_p10,
       ADDRESS_RANGE_FBOX_active_address_out_of_range, DATAPATH_INSTANCE_negative, DATAPATH_INSTANCE_zero,
       EFFECTIVE_ADDRESS_FBOX_p4, EFFECTIVE_ADDRESS_FBOX_p12, EFFECTIVE_ADDRESS_FBOX_p14,
       EFFECTIVE_ADDRESS_FBOX_p15, FETCH_DECODE_CONTROLS_acc_memory_request,
       FETCH_DECODE_CONTROLS_add_operand, FETCH_DECODE_CONTROLS_addr_reg_argument,
       FETCH_DECODE_CONTROLS_addr_reg_offs_argument, FETCH_DECODE_CONTROLS_and_operand,
       FETCH_DECODE_CONTROLS_div_operand, FETCH_DECODE_CONTROLS_jump_adr, FETCH_DECODE_CONTROLS_jump_error,
       FETCH_DECODE_CONTROLS_jump_negative, FETCH_DECODE_CONTROLS_jump_not_error,
       FETCH_DECODE_CONTROLS_jump_not_zero, FETCH_DECODE_CONTROLS_jump_zero,
       FETCH_DECODE_CONTROLS_ld_reg_adr, FETCH_DECODE_CONTROLS_ld_reg_const, FETCH_DECODE_CONTROLS_load_adr,
       FETCH_DECODE_CONTROLS_load_const, FETCH_DECODE_CONTROLS_load_reg_off,
       FETCH_DECODE_CONTROLS_mul_operand, FETCH_DECODE_CONTROLS_not, FETCH_DECODE_CONTROLS_or_operand,
       FETCH_DECODE_CONTROLS_set_ovf, FETCH_DECODE_CONTROLS_sub_operand, FETCH_DECODE_CONTROLS_xor_operand,
       FETCH_DECODE_halt_error, FETCH_DECODE_jump_not_zero, JUMP_BOX_dec_jump_not_zero, JUMP_BOX_is_not_zero,
       MEMORY_INSTANCE_p1, MEMORY_WRITE_REQUEST_out, OPERATIONS_INSTANCE_p15, OPERATIONS_INSTANCE_p18,
       OPERATIONS_INSTANCE_p19, OPERATIONS_INSTANCE_p20, OPERATIONS_INSTANCE_p21, undriven_2;
  wire [5:0] undriven;
  wire [7:0] FETCH_DECODE_pc_out, OPERATIONS_INSTANCE_p17;
  wire [13:0] FETCH_DECODE_opcode;
  wire [15:0] multiplexer_1_out;
  wire [15:6] MEMORY_INSTANCE_p7;
  wire [15:14] EFFECTIVE_ADDRESS_FBOX_p1;

  or MEMORY_WRITE_REQUEST (MEMORY_WRITE_REQUEST_out, PRINT_ADDRESS_ENABLE, PRINT_ENABLE, HALTED);
  FetchDecode FETCH_DECODE (
    .CLK(CLK), .RESET(RESET), .DEC_JUMP_NOT_ZERO(JUMP_BOX_is_not_zero),
    .NOT_ZERO(JUMP_BOX_dec_jump_not_zero), .PROGRAM_LIMIT({8{1'b1}}), .DEC_HALT_ERROR(1'b1),
    .JUMP_NOT_ZERO(FETCH_DECODE_jump_not_zero), .HALT_ERROR(FETCH_DECODE_halt_error),
    .PC_OUT(FETCH_DECODE_pc_out), .OPCODE(FETCH_DECODE_opcode));
  // Memory MEMORY_INSTANCE: pin names not known; wires that end beside it: MEMORY_INSTANCE_p1, MEMORY_WRITE_REQUEST_out, CLK, PRINT_VALID, PRINT_VALUE, PRINT_ADDRESS_VALID, {MEMORY_INSTANCE_p7, PRINT_ADDRESS_VALUE}
  // Probe on FETCH_DECODE_jump_not_zero
  // Probe on FETCH_DECODE_halt_error
  // Probe on FETCH_DECODE_pc_out
  // AddressPath ADDRESS_PATH: pin names not known; wires that end beside it: 16'h1, ADDRESS_PATH_p2, 16'h1, 1'b1, CLK, 1'b1, ADDRESS_PATH_p7, ADDRESS_PATH_p8, ADDRESS_PATH_p9, ADDRESS_PATH_p10
  FetchDecodeControls FETCH_DECODE_CONTROLS (
    .OPCODE(undriven), .ADD_OPERAND(FETCH_DECODE_CONTROLS_add_operand),
    .SUB_OPERAND(FETCH_DECODE_CONTROLS_sub_operand), .MUL_OPERAND(FETCH_DECODE_CONTROLS_mul_operand),
    .DIV_OPERAND(FETCH_DECODE_CONTROLS_div_operand), .AND_OPERAND(FETCH_DECODE_CONTROLS_and_operand),
    .OR_OPERAND(FETCH_DECODE_CONTROLS_or_operand), .XOR_OPERAND(FETCH_DECODE_CONTROLS_xor_operand),
    .ADDR_REG_ARGUMENT(FETCH_DECODE_CONTROLS_addr_reg_argument),
    .ADDR_REG_OFFS_ARGUMENT(FETCH_DECODE_CONTROLS_addr_reg_offs_argument), .NOT(FETCH_DECODE_CONTROLS_not),
    .JUMP_ADR(FETCH_DECODE_CONTROLS_jump_adr), .JUMP_ZERO(FETCH_DECODE_CONTROLS_jump_zero),
    .JUMP_NOT_ZERO(FETCH_DECODE_CONTROLS_jump_not_zero), .JUMP_NEGATIVE(FETCH_DECODE_CONTROLS_jump_negative),
    .JUMP_ERROR(FETCH_DECODE_CONTROLS_jump_error), .JUMP_NOT_ERROR(FETCH_DECODE_CONTROLS_jump_not_error),
    .LOAD_CONST(FETCH_DECODE_CONTROLS_load_const), .LOAD_ADR(FETCH_DECODE_CONTROLS_load_adr),
    .LOAD_REG_OFF(FETCH_DECODE_CONTROLS_load_reg_off), .LD_REG_CONST(FETCH_DECODE_CONTROLS_ld_reg_const),
    .LD_REG_ADR(FETCH_DECODE_CONTROLS_ld_reg_adr), .SET_OVF(FETCH_DECODE_CONTROLS_set_ovf),
    .SET_DIV0(PRINT_ENABLE), .SET_ADDR(PRINT_ADDRESS_ENABLE), .SET_INV(HALTED), .SET_ILL(HALTED_WITH_ERROR),
    .ACC_MEMORY_REQUEST(FETCH_DECODE_CONTROLS_acc_memory_request), .ACC_WRITE_REQUEST(ADDRESS_PATH_p2));  // open: CONST_ARGUMENT, ADDR_ARGUMENT, LOAD_ADR_REG, STORE_ADR, STORE_ADR_REG, STORE_REG_OFF, SET_INPUT, CLEAR_ERROR, INPUT, PRINT, PRINT_ADR, HALT, HALT_ERROR, INVALID_OPERAND
  // Probe on FETCH_DECODE_CONTROLS_jump_not_zero
  // Probe on FETCH_DECODE_CONTROLS_jump_negative
  // Probe on FETCH_DECODE_CONTROLS_jump_not_error
  // Probe on FETCH_DECODE_CONTROLS_load_const
  // Probe on FETCH_DECODE_CONTROLS_load_adr
  // Probe on FETCH_DECODE_CONTROLS_load_reg_off
  // Probe on FETCH_DECODE_CONTROLS_ld_reg_const
  // Probe on FETCH_DECODE_CONTROLS_ld_reg_adr
  // Probe on FETCH_DECODE_CONTROLS_set_ovf
  Datapath DATAPATH_INSTANCE (
    .DATA_IN(OPERATIONS_INSTANCE_p17), .DATAPATH_STARTUP_RESET(1'b0), .ACC_LOAD(ADDRESS_PATH_p2),
    .VALID_IN(OPERATIONS_INSTANCE_p18), .CLK(CLK), .ACC_OUT(PRINT_VALUE[7:0]), .ZERO(DATAPATH_INSTANCE_zero),
    .NEGATIVE(DATAPATH_INSTANCE_negative), .ACC_VALID_OUT(PRINT_VALID));
  Multiplexer #(.width(16)) multiplexer_1 (
    .in0({EFFECTIVE_ADDRESS_FBOX_p1, FETCH_DECODE_opcode}), .in1({MEMORY_INSTANCE_p7, PRINT_ADDRESS_VALUE}),
    .out(multiplexer_1_out), .sel(FETCH_DECODE_CONTROLS_acc_memory_request));
  ErrorFlags ERROR_FLAGS (
    .CLK(CLK), .SET_OVF(OPERATIONS_INSTANCE_p18), .SET_DIV0(OPERATIONS_INSTANCE_p21),
    .SET_ADDR(ADDRESS_RANGE_FBOX_active_address_out_of_range), .SET_INV(OPERATIONS_INSTANCE_p20),
    .OVF_OUT(ERROR_OVF), .DIV0_OUT(ERROR_DIV0), .ADDR_OUT(ERROR_ADDR), .INV_OUT(ERROR_INV),
    .ILL_OUT(ERROR_ILL), .INPUT_OUT(ERROR_INPUT));  // open: CLEAR_ERROR, SET_ILL, SET_INPUT
  // Operations OPERATIONS_INSTANCE: pin names not known; wires that end beside it: PRINT_VALUE, multiplexer_1_out, {MEMORY_INSTANCE_p7, PRINT_ADDRESS_VALUE}, PRINT_ADDRESS_VALID, PRINT_VALID, FETCH_DECODE_CONTROLS_addr_reg_argument, FETCH_DECODE_CONTROLS_add_operand, FETCH_DECODE_CONTROLS_sub_operand, FETCH_DECODE_CONTROLS_mul_operand, FETCH_DECODE_CONTROLS_div_operand, FETCH_DECODE_CONTROLS_and_operand, FETCH_DECODE_CONTROLS_or_operand, FETCH_DECODE_CONTROLS_xor_operand, FETCH_DECODE_CONTROLS_jump_zero, OPERATIONS_INSTANCE_p15, OPERATIONS_INSTANCE_p15, OPERATIONS_INSTANCE_p17, OPERATIONS_INSTANCE_p18, OPERATIONS_INSTANCE_p19, OPERATIONS_INSTANCE_p20, OPERATIONS_INSTANCE_p21
  // EffectiveAddress EFFECTIVE_ADDRESS_FBOX: pin names not known; wires that end beside it: {EFFECTIVE_ADDRESS_FBOX_p1, FETCH_DECODE_opcode}, ADDRESS_PATH_p7, FETCH_DECODE_CONTROLS_addr_reg_offs_argument, EFFECTIVE_ADDRESS_FBOX_p4, ADDRESS_PATH_p8, FETCH_DECODE_CONTROLS_jump_adr, PRINT_ENABLE, PRINT_ADDRESS_ENABLE, HALTED, HALTED_WITH_ERROR, EFFECTIVE_ADDRESS_FBOX_p4, EFFECTIVE_ADDRESS_FBOX_p12, MEMORY_INSTANCE_p1, EFFECTIVE_ADDRESS_FBOX_p14, EFFECTIVE_ADDRESS_FBOX_p15
  AddressRangeFBox ADDRESS_RANGE_FBOX (
    .OFFSET_CARRY(ADDRESS_PATH_p9), .EFFECTIVE_REGISTER_MODE(EFFECTIVE_ADDRESS_FBOX_p12),
    .EFFECTIVE_OFFSET_MODE(EFFECTIVE_ADDRESS_FBOX_p14), .ADDRESS_OUT_OF_RANGE(EFFECTIVE_ADDRESS_FBOX_p15),
    .LOAD_ADDRESS(FETCH_DECODE_CONTROLS_not),
    .ACTIVE_ADDRESS_OUT_OF_RANGE(ADDRESS_RANGE_FBOX_active_address_out_of_range));  // open: ADD_ADDRESS, SUB_ADDRESS, MUL_ADDRESS, DIV_ADDRESS, AND_ADDRESS, OR_ADDRESS, STORE_ADDRESS
  // Probe on ADDRESS_PATH_p10
  // Probe on FETCH_DECODE_CONTROLS_acc_memory_request
  // Probe on undriven_2
  // Probe on nothing
  // Probe on OPERATIONS_INSTANCE_p19
  // Probe on EFFECTIVE_ADDRESS_FBOX_p4
  // Probe on MEMORY_INSTANCE_p1
  JumpBox JUMP_BOX (
    .ERROR_OVF(ERROR_OVF), .ERROR_DIV0(ERROR_DIV0), .ERROR_ADDR(ERROR_ADDR), .ERROR_INV(ERROR_INV),
    .ERROR_ILL(ERROR_ILL), .ERROR_INPUT(ERROR_INPUT), .JUMP_ADR(FETCH_DECODE_CONTROLS_jump_not_zero),
    .JUMP_ZERO(FETCH_DECODE_CONTROLS_jump_negative), .JUMP_NOT_ZERO(FETCH_DECODE_CONTROLS_jump_error),
    .JUMP_NEGATIVE(FETCH_DECODE_CONTROLS_jump_not_error), .JUMP_ERROR(FETCH_DECODE_CONTROLS_load_const),
    .JUMP_NOT_ERROR(FETCH_DECODE_CONTROLS_load_adr), .NEGATIVE(DATAPATH_INSTANCE_negative),
    .ZERO(DATAPATH_INSTANCE_zero), .IS_NOT_ZERO(JUMP_BOX_is_not_zero),
    .DEC_JUMP_NOT_ZERO(JUMP_BOX_dec_jump_not_zero));
  // Pins of 14 and 16 bits meet at {EFFECTIVE_ADDRESS_FBOX_p1, FETCH_DECODE_opcode}
  // Pins of 8 and 16 bits meet at PRINT_VALUE
  // Pins of 6 and 16 bits meet at {MEMORY_INSTANCE_p7, PRINT_ADDRESS_VALUE}
endmodule

module EffectiveAddress (
  input  [7:0] DIRECT_ADDR,
  input  [7:0] REG_ADDR,
  input  LOAD_ADR_REG,
  input  ADD_ADR_REG,
  input  SUB_ADR_REG,
  input  MUL_ADR_REG,
  input  DIV_ADR_REG,
  input  AND_ADR_REG,
  input  OR_ADR_REG,
  input  STORE_ADR_REG,
  input  [7:0] OFFSET_ADDR,
  input  [7:0] REG_SELECTED,
  input  LOAD_REG_OFF,
  input  ADD_REG_OFF,
  input  SUB_REG_OFF,
  input  MUL_REG_OFF,
  input  DIV_REG_OFF,
  input  AND_REG_OFF,
  input  OR_REG_OFF,
  input  STORE_REG_OFF,
  output [7:0] EFFECTIVE_REGISTER_SELECTED_OUT,
  output EFFECTIVE_REGISTER_MODE,
  output [7:0] EFFECTIVE_MEMORY_ADDRESS,
  output EFFECTIVE_OFFSET_MODE,
  output ADDRESS_OUT_OF_RANGE
);

  or MEMORY_ADDRESS_REGISTER_SELECT (EFFECTIVE_REGISTER_MODE, LOAD_ADR_REG, ADD_ADR_REG, SUB_ADR_REG, MUL_ADR_REG, DIV_ADR_REG, AND_ADR_REG, OR_ADR_REG, STORE_ADR_REG);
  or MEMORY_ADDRESS_OFFSET_SELECT (EFFECTIVE_OFFSET_MODE, LOAD_REG_OFF, ADD_REG_OFF, SUB_REG_OFF, MUL_REG_OFF, DIV_REG_OFF, AND_REG_OFF, OR_REG_OFF, STORE_REG_OFF);
  Multiplexer #(.width(8)) multiplexer_1 (
    .in0(DIRECT_ADDR), .in1(REG_ADDR), .out(EFFECTIVE_REGISTER_SELECTED_OUT), .sel(EFFECTIVE_REGISTER_MODE));
  Multiplexer #(.width(8)) multiplexer_2 (
    .in0(OFFSET_ADDR), .in1(REG_SELECTED), .out(EFFECTIVE_MEMORY_ADDRESS), .sel(EFFECTIVE_OFFSET_MODE));
  Comparator comparator_1 (.a(EFFECTIVE_MEMORY_ADDRESS), .b({8{1'b1}}), .gt(ADDRESS_OUT_OF_RANGE));  // open: eq, lt
endmodule

module Datapath (
  input  [7:0] DATA_IN,
  input  DATAPATH_STARTUP_RESET,
  input  ACC_LOAD,
  input  VALID_IN,
  input  CLK,
  output [7:0] ACC_OUT,
  output ZERO,
  output NEGATIVE,
  output ACC_VALID_OUT
);

  Register ACC (.D(DATA_IN), .en(ACC_LOAD), .clk(CLK), .Q(ACC_OUT), .clr(DATAPATH_STARTUP_RESET));
  Register #(.width(1)) ACC_VALID (
    .D(VALID_IN), .en(ACC_LOAD), .clk(CLK), .Q(ACC_VALID_OUT), .clr(DATAPATH_STARTUP_RESET));
  Comparator comparator_1 (.a(ACC_OUT), .b({8{1'b0}}), .eq(ZERO), .lt(NEGATIVE));  // open: gt

  // Notes on the sheet:
  //   Clocked 16-bit accumulator; signed comparator derives ZERO and NEGATIVE
endmodule

module AddressPath (
  input  [7:0] ADDRESS_IN,
  input  AR_LOAD,
  input  [7:0] OFFSET,
  input  VALID_IN,
  input  CLK,
  input  ADDRESS_PATH_STARTUP_RESET,
  output [7:0] ADDRESS,
  output [7:0] ADDRESS_PLUS_OFFSET,
  output OFFSET_CARRY,
  output ADDRESS_VALID
);

  Register AR (.D(ADDRESS_IN), .en(AR_LOAD), .clk(CLK), .Q(ADDRESS), .clr(ADDRESS_PATH_STARTUP_RESET));
  Register #(.width(1)) AR_VALID (
    .D(VALID_IN), .en(AR_LOAD), .clk(CLK), .Q(ADDRESS_VALID), .clr(ADDRESS_PATH_STARTUP_RESET));
  Adder adder_1 (.a(ADDRESS), .b(OFFSET), .out(ADDRESS_PLUS_OFFSET), .cout(OFFSET_CARRY));  // open: cin

  // Notes on the sheet:
  //   Clocked 12-bit address register with combinational offset addition
endmodule

module Memory (
  input  [7:0] ADDRESS,
  input  WRITE_ENABLE,
  input  CLK,
  input  VALID_IN,
  input  [7:0] DATA_IN,
  output MEMORY_VALID,
  output [7:0] MEMORY_DATA
);

  RAM #(.asyncread("true"), .dataWidth(1)) VALID_RAM (
    .addr(ADDRESS), .we(WRITE_ENABLE), .oe(1'b1), .clk(CLK), .din(VALID_IN), .dout(MEMORY_VALID));
  RAM #(.asyncread("true")) DATA_RAM (
    .addr(ADDRESS), .we(WRITE_ENABLE), .oe(1'b1), .clk(CLK), .din(DATA_IN), .dout(MEMORY_DATA));

  // Notes on the sheet:
  //   256-word value/valid memory with shared address, write-enable, and clock
endmodule

module ErrorFlags (
  input  CLEAR_ERROR,
  input  CLK,
  input  SET_OVF,
  input  SET_DIV0,
  input  SET_ADDR,
  input  SET_INV,
  input  SET_ILL,
  input  SET_INPUT,
  output OVF_OUT,
  output DIV0_OUT,
  output ADDR_OUT,
  output INV_OUT,
  output ILL_OUT,
  output INPUT_OUT
);

  wire HOLD_ADDR_out, HOLD_DIV0_out, HOLD_ILL_out, HOLD_INPUT_out, HOLD_INV_out, HOLD_OVF_out, NEXT_ADDR_out,
       NEXT_DIV0_out, NEXT_ILL_out, NEXT_INPUT_out, NEXT_INV_out, NEXT_OVF_out, NOT_CLEAR_ERROR_out;

  not NOT_CLEAR_ERROR (NOT_CLEAR_ERROR_out, CLEAR_ERROR);
  and HOLD_OVF (HOLD_OVF_out, OVF_OUT, NOT_CLEAR_ERROR_out);
  and HOLD_DIV0 (HOLD_DIV0_out, DIV0_OUT, NOT_CLEAR_ERROR_out);
  and HOLD_INV (HOLD_INV_out, INV_OUT, NOT_CLEAR_ERROR_out);
  or NEXT_DIV0 (NEXT_DIV0_out, SET_DIV0, HOLD_DIV0_out);
  and HOLD_ADDR (HOLD_ADDR_out, ADDR_OUT, NOT_CLEAR_ERROR_out);
  and HOLD_ILL (HOLD_ILL_out, ILL_OUT, NOT_CLEAR_ERROR_out);
  and HOLD_INPUT (HOLD_INPUT_out, INPUT_OUT, NOT_CLEAR_ERROR_out);
  or NEXT_OVF (NEXT_OVF_out, SET_OVF, HOLD_OVF_out);
  or NEXT_ADDR (NEXT_ADDR_out, SET_ADDR, HOLD_ADDR_out);
  or NEXT_INV (NEXT_INV_out, SET_INV, HOLD_INV_out);
  or NEXT_ILL (NEXT_ILL_out, SET_ILL, HOLD_ILL_out);
  or NEXT_INPUT (NEXT_INPUT_out, SET_INPUT, HOLD_INPUT_out);
  Register #(.width(1)) OVF (.D(NEXT_OVF_out), .en(1'b1), .clk(CLK), .Q(OVF_OUT), .clr(CLEAR_ERROR));
  Register #(.width(1)) DIV0 (.D(NEXT_DIV0_out), .en(1'b1), .clk(CLK), .Q(DIV0_OUT), .clr(CLEAR_ERROR));
  Register #(.width(1)) ADDR (.D(NEXT_ADDR_out), .en(1'b1), .clk(CLK), .Q(ADDR_OUT), .clr(CLEAR_ERROR));
  Register #(.width(1)) INV (.D(NEXT_INV_out), .en(1'b1), .clk(CLK), .Q(INV_OUT), .clr(CLEAR_ERROR));
  Register #(.width(1)) ILL (.D(NEXT_ILL_out), .en(1'b1), .clk(CLK), .Q(ILL_OUT), .clr(CLEAR_ERROR));
  Register #(.width(1)) INPUT (.D(NEXT_INPUT_out), .en(1'b1), .clk(CLK), .Q(INPUT_OUT), .clr(CLEAR_ERROR));

  // Notes on the sheet:
  //   Set-dominant sticky flags: SET OR (current AND NOT CLEAR_ERROR)
endmodule

module FetchDecode (
  input  CLK,
  input  RESET,
  input  DEC_JUMP_NOT_ZERO,
  input  NOT_ZERO,
  input  [7:0] PROGRAM_LIMIT,
  input  DEC_HALT_ERROR,
  output JUMP_NOT_ZERO,
  output HALT_ERROR,
  output [7:0] PC_OUT,
  output [13:0] OPCODE
);


  // Notes on the sheet:
  //   PROGRAM_LIMIT: initial=0xfff
endmodule

module FetchDecodeControls (
  input  [5:0] OPCODE,
  output ADD_OPERAND,
  output SUB_OPERAND,
  output MUL_OPERAND,
  output DIV_OPERAND,
  output AND_OPERAND,
  output OR_OPERAND,
  output XOR_OPERAND,
  output CONST_ARGUMENT,
  output ADDR_ARGUMENT,
  output ADDR_REG_ARGUMENT,
  output ADDR_REG_OFFS_ARGUMENT,
  output NOT,
  output JUMP_ADR,
  output JUMP_ZERO,
  output JUMP_NOT_ZERO,
  output JUMP_NEGATIVE,
  output JUMP_ERROR,
  output JUMP_NOT_ERROR,
  output LOAD_CONST,
  output LOAD_ADR,
  output LOAD_ADR_REG,
  output LOAD_REG_OFF,
  output LD_REG_CONST,
  output LD_REG_ADR,
  output STORE_ADR,
  output STORE_ADR_REG,
  output STORE_REG_OFF,
  output SET_OVF,
  output SET_DIV0,
  output SET_ADDR,
  output SET_INV,
  output SET_ILL,
  output SET_INPUT,
  output CLEAR_ERROR,
  output INPUT,
  output PRINT,
  output PRINT_ADR,
  output HALT,
  output HALT_ERROR,
  output INVALID_OPERAND,
  output ACC_MEMORY_REQUEST,
  output ACC_WRITE_REQUEST
);
endmodule

module IntegrationClock (
  input  CLK,
  output FETCH_CLK,
  output DATAPATH_CLK,
  output ADDRESS_CLK,
  output MEMORY_CLK,
  output ERROR_FLAGS_CLK
);


  assign ADDRESS_CLK = CLK;
  assign DATAPATH_CLK = CLK;
  assign ERROR_FLAGS_CLK = CLK;
  assign FETCH_CLK = CLK;
  assign MEMORY_CLK = CLK;
endmodule

module IntegrationReset (
  input  RESET,
  output FETCH_RESET
);


  assign FETCH_RESET = RESET;
endmodule

module AndArithmeticCircuit (
  input  AND_ACTIVATED,
  input  [7:0] LEFT,
  input  [7:0] RIGHT,
  input  INPUT_VALID,
  output [7:0] RESULT,
  output RESULT_VALID
);
endmodule

module AndSubCircuit (
  input  AND_CONST,
  input  AND_ADDRESS,
  input  AND_ADDRESS_REGISTER,
  input  AND_ADDRESS_REGISTER_PLUS_OFFSET,
  input  [7:0] ACC_VALUE,
  input  [7:0] MEMORY_VALUE,
  input  [7:0] IMMEDIATE_VALUE,
  input  MEMORY_VALID,
  input  ACC_VALID,
  output [7:0] RESULT,
  output RESULT_VALID,
  output RESULT_ACTIVE
);

  wire ACC_AND_VALID_out, multiplexer_2_out;
  wire [7:0] multiplexer_1_out;

  or ACC_AND_MEMORY_SELECT (RESULT_ACTIVE, AND_CONST, AND_ADDRESS, AND_ADDRESS_REGISTER, AND_ADDRESS_REGISTER_PLUS_OFFSET);
  Multiplexer #(.width(8)) multiplexer_1 (
    .in0(MEMORY_VALUE), .in1(IMMEDIATE_VALUE), .out(multiplexer_1_out), .sel(AND_CONST));
  Multiplexer multiplexer_2 (.in0(1'b1), .in1(MEMORY_VALID), .out(multiplexer_2_out), .sel(AND_CONST));
  and ACC_AND_VALID (ACC_AND_VALID_out, multiplexer_2_out, ACC_VALID);
  AndArithmeticCircuit ANDARITHMETICCIRCUIT_1300_440 (
    .AND_ACTIVATED(RESULT_ACTIVE), .LEFT(ACC_VALUE), .RIGHT(multiplexer_1_out),
    .INPUT_VALID(ACC_AND_VALID_out), .RESULT(RESULT), .RESULT_VALID(RESULT_VALID));

  // Notes on the sheet:
  //   MEMORY_VALID →
  //   AND_VALID →
  //   CONST_VALID →
endmodule

module Operations (
  input  [7:0] ACC_VALUE,
  input  [7:0] MEMORY_VALUE,
  input  [7:0] IMMEDIATE_VALUE,
  input  MEMORY_VALID,
  input  ACC_VALID,
  input  CONST_OPERAND,
  input  ADD_OPERAND,
  input  SUB_OPERAND,
  input  MUL_OPERAND,
  input  DIV_OPERAND,
  input  AND_OPERAND,
  input  OR_OPERAND,
  input  XOR_OPERAND,
  input  NOT_OPERAND,
  output [7:0] RESULT_VALUE,
  output OVERFLOW,
  output RESULT_IS_VALID,
  output INVALID_OPERAND,
  output DIVIDE_BY_ZERO
);
endmodule

module NotCircuit (
  input  NOT_IS_ACTIVE,
  input  [7:0] ACC_VALUE,
  input  ACC_VALID,
  output [7:0] RESULT,
  output RESULT_VALID
);
endmodule

module DecodeSignals (
  input  [5:0] Opcode,
  output ACC_MEMORY_REQUEST,
  output ACC_WRITE_REQUEST
);

  wire ACC_LOAD_REQUEST_out, CONTROL_DECODER_acc_memory_request, CONTROL_DECODER_acc_write_request,
       CONTROL_DECODER_add_operand, CONTROL_DECODER_addr_argument, CONTROL_DECODER_addr_reg_argument,
       CONTROL_DECODER_addr_reg_offs_argument, CONTROL_DECODER_and_operand, CONTROL_DECODER_clear_error,
       CONTROL_DECODER_const_argument, CONTROL_DECODER_div_operand, CONTROL_DECODER_halt,
       CONTROL_DECODER_halt_error, CONTROL_DECODER_input, CONTROL_DECODER_invalid_operand,
       CONTROL_DECODER_jump_adr, CONTROL_DECODER_jump_error, CONTROL_DECODER_jump_negative,
       CONTROL_DECODER_jump_not_error, CONTROL_DECODER_jump_not_zero, CONTROL_DECODER_jump_zero,
       CONTROL_DECODER_ld_reg_adr, CONTROL_DECODER_ld_reg_const, CONTROL_DECODER_load_adr,
       CONTROL_DECODER_load_adr_reg, CONTROL_DECODER_load_const, CONTROL_DECODER_load_reg_off,
       CONTROL_DECODER_mul_operand, CONTROL_DECODER_not, CONTROL_DECODER_or_operand, CONTROL_DECODER_print,
       CONTROL_DECODER_print_adr, CONTROL_DECODER_set_addr, CONTROL_DECODER_set_div0,
       CONTROL_DECODER_set_ill, CONTROL_DECODER_set_input, CONTROL_DECODER_set_inv, CONTROL_DECODER_set_ovf,
       CONTROL_DECODER_store_adr, CONTROL_DECODER_store_adr_reg, CONTROL_DECODER_store_reg_off,
       CONTROL_DECODER_sub_operand, CONTROL_DECODER_xor_operand, undriven, undriven_2, undriven_3,
       undriven_4, undriven_5, undriven_6, undriven_7, undriven_8, undriven_9, undriven_10, undriven_11,
       undriven_12, undriven_13, undriven_14;

  FetchDecodeControls CONTROL_DECODER (
    .OPCODE(Opcode), .ADD_OPERAND(CONTROL_DECODER_add_operand), .SUB_OPERAND(CONTROL_DECODER_sub_operand),
    .MUL_OPERAND(CONTROL_DECODER_mul_operand), .DIV_OPERAND(CONTROL_DECODER_div_operand),
    .AND_OPERAND(CONTROL_DECODER_and_operand), .OR_OPERAND(CONTROL_DECODER_or_operand),
    .XOR_OPERAND(CONTROL_DECODER_xor_operand), .CONST_ARGUMENT(CONTROL_DECODER_const_argument),
    .ADDR_ARGUMENT(CONTROL_DECODER_addr_argument), .ADDR_REG_ARGUMENT(CONTROL_DECODER_addr_reg_argument),
    .ADDR_REG_OFFS_ARGUMENT(CONTROL_DECODER_addr_reg_offs_argument), .NOT(CONTROL_DECODER_not),
    .JUMP_ADR(CONTROL_DECODER_jump_adr), .JUMP_ZERO(CONTROL_DECODER_jump_zero),
    .JUMP_NOT_ZERO(CONTROL_DECODER_jump_not_zero), .JUMP_NEGATIVE(CONTROL_DECODER_jump_negative),
    .JUMP_ERROR(CONTROL_DECODER_jump_error), .JUMP_NOT_ERROR(CONTROL_DECODER_jump_not_error),
    .LOAD_CONST(CONTROL_DECODER_load_const), .LOAD_ADR(CONTROL_DECODER_load_adr),
    .LOAD_ADR_REG(CONTROL_DECODER_load_adr_reg), .LOAD_REG_OFF(CONTROL_DECODER_load_reg_off),
    .LD_REG_CONST(CONTROL_DECODER_ld_reg_const), .LD_REG_ADR(CONTROL_DECODER_ld_reg_adr),
    .STORE_ADR(CONTROL_DECODER_store_adr), .STORE_ADR_REG(CONTROL_DECODER_store_adr_reg),
    .STORE_REG_OFF(CONTROL_DECODER_store_reg_off), .SET_OVF(CONTROL_DECODER_set_ovf),
    .SET_DIV0(CONTROL_DECODER_set_div0), .SET_ADDR(CONTROL_DECODER_set_addr),
    .SET_INV(CONTROL_DECODER_set_inv), .SET_ILL(CONTROL_DECODER_set_ill),
    .SET_INPUT(CONTROL_DECODER_set_input), .CLEAR_ERROR(CONTROL_DECODER_clear_error),
    .INPUT(CONTROL_DECODER_input), .PRINT(CONTROL_DECODER_print), .PRINT_ADR(CONTROL_DECODER_print_adr),
    .HALT(CONTROL_DECODER_halt), .HALT_ERROR(CONTROL_DECODER_halt_error),
    .INVALID_OPERAND(CONTROL_DECODER_invalid_operand),
    .ACC_MEMORY_REQUEST(CONTROL_DECODER_acc_memory_request),
    .ACC_WRITE_REQUEST(CONTROL_DECODER_acc_write_request));
  // Probe on CONTROL_DECODER_jump_not_zero
  // Probe on CONTROL_DECODER_store_adr
  // Probe on CONTROL_DECODER_store_adr_reg
  // Probe on CONTROL_DECODER_store_reg_off
  // Probe on CONTROL_DECODER_set_ovf
  // Probe on CONTROL_DECODER_set_div0
  // Probe on CONTROL_DECODER_set_addr
  // Probe on CONTROL_DECODER_set_inv
  // Probe on CONTROL_DECODER_set_ill
  // Probe on CONTROL_DECODER_set_input
  // Probe on CONTROL_DECODER_input
  // Probe on CONTROL_DECODER_print
  // Probe on CONTROL_DECODER_print_adr
  // Probe on CONTROL_DECODER_halt
  // Probe on CONTROL_DECODER_halt_error
  // Probe on CONTROL_DECODER_invalid_operand
  // Probe on CONTROL_DECODER_acc_write_request
  // Probe on undriven
  // Probe on undriven_2
  // Probe on undriven_3
  // Probe on undriven_4
  // Probe on undriven_5
  // Probe on undriven_6
  // Probe on undriven_7
  // Probe on undriven_8
  // Probe on undriven_9
  // Probe on undriven_10
  // Probe on undriven_11
  // Probe on undriven_12
  // Probe on undriven_13
  // Probe on undriven_14
  or ACC_LOAD_REQUEST (ACC_LOAD_REQUEST_out, CONTROL_DECODER_add_operand, CONTROL_DECODER_sub_operand, CONTROL_DECODER_mul_operand, CONTROL_DECODER_div_operand, CONTROL_DECODER_and_operand, CONTROL_DECODER_or_operand, CONTROL_DECODER_xor_operand, CONTROL_DECODER_const_argument, CONTROL_DECODER_addr_argument, CONTROL_DECODER_addr_reg_argument, CONTROL_DECODER_addr_reg_offs_argument, CONTROL_DECODER_not, CONTROL_DECODER_jump_adr, CONTROL_DECODER_jump_zero, CONTROL_DECODER_jump_negative, CONTROL_DECODER_jump_error, CONTROL_DECODER_jump_not_error, CONTROL_DECODER_load_const, CONTROL_DECODER_load_adr, CONTROL_DECODER_load_adr_reg, CONTROL_DECODER_load_reg_off, CONTROL_DECODER_ld_reg_const, CONTROL_DECODER_ld_reg_adr, CONTROL_DECODER_store_adr, CONTROL_DECODER_store_adr_reg, CONTROL_DECODER_store_reg_off, CONTROL_DECODER_set_ovf);
  or ACC_MEMORY_SELECT (ACC_MEMORY_REQUEST, CONTROL_DECODER_and_operand, CONTROL_DECODER_mul_operand, CONTROL_DECODER_div_operand);
  or ACC_WRITE_AGGREGATOR (ACC_WRITE_REQUEST, ACC_LOAD_REQUEST_out, CONTROL_DECODER_clear_error, CONTROL_DECODER_acc_memory_request);
endmodule

module AddSubCircuit (
  input  ADD_CONST,
  input  ADD_ADDRESS,
  input  ADD_ADDRESS_REGISTER,
  input  ADD_ADDRESS_REGISTER_PLUS_OFFSET,
  input  [7:0] ACC_VALUE,
  input  [7:0] MEMORY_VALUE,
  input  [7:0] IMMEDIATE_VALUE,
  input  MEMORY_VALID,
  input  ACC_VALID,
  output [7:0] RESULT,
  output OVERFLOW,
  output RESULT_VALID,
  output RESULT_ACTIVE
);

  wire ACC_ADD_VALID_out, multiplexer_2_out;
  wire [7:0] multiplexer_1_out;

  Multiplexer #(.width(8)) multiplexer_1 (
    .in0(MEMORY_VALUE), .in1(IMMEDIATE_VALUE), .out(multiplexer_1_out), .sel(ADD_CONST));
  Multiplexer multiplexer_2 (.in0(1'b1), .in1(MEMORY_VALID), .out(multiplexer_2_out), .sel(ADD_CONST));
  or ACC_ADD_MEMORY_SELECT (RESULT_ACTIVE, ADD_CONST, ADD_ADDRESS, ADD_ADDRESS_REGISTER, ADD_ADDRESS_REGISTER_PLUS_OFFSET);
  and ACC_ADD_VALID (ACC_ADD_VALID_out, multiplexer_2_out, ACC_VALID);
  AddArithmeticCircuit ADDARITHMETICCIRCUIT_1300_440 (
    .ADD_ACTIVATED(RESULT_ACTIVE), .LEFT(ACC_VALUE), .RIGHT(multiplexer_1_out),
    .INPUT_VALID(ACC_ADD_VALID_out), .RESULT(RESULT), .OVERFLOW(OVERFLOW), .RESULT_VALID(RESULT_VALID));

  // Notes on the sheet:
  //   MEMORY_VALID →
  //   ADD_VALID →
  //   CONST_VALID →
endmodule

module SubSubCircuit (
  input  SUB_CONST,
  input  SUB_ADDRESS_REGISTER_PLUS_OFFSET,
  input  SUB_ADDRESS,
  input  SUB_ADDRESS_REGISTER,
  input  [7:0] ACC_VALUE,
  input  [7:0] MEMORY_VALUE,
  input  [7:0] IMMEDIATE_VALUE,
  input  MEMORY_VALID,
  input  ACC_VALID,
  output [7:0] RESULT,
  output OVERFLOW,
  output RESULT_VALID,
  output RESULT_ACTIVE
);

  wire ACC_SUB_VALID_out, multiplexer_2_out;
  wire [7:0] multiplexer_1_out;

  or ACC_SUB_MEMORY_SELECT (RESULT_ACTIVE, SUB_CONST, SUB_ADDRESS_REGISTER_PLUS_OFFSET, SUB_ADDRESS, SUB_ADDRESS_REGISTER);
  Multiplexer #(.width(8)) multiplexer_1 (
    .in0(MEMORY_VALUE), .in1(IMMEDIATE_VALUE), .out(multiplexer_1_out), .sel(SUB_CONST));
  Multiplexer multiplexer_2 (.in0(1'b1), .in1(MEMORY_VALID), .out(multiplexer_2_out), .sel(SUB_CONST));
  and ACC_SUB_VALID (ACC_SUB_VALID_out, multiplexer_2_out, ACC_VALID);
  SubArithmeticCircuit SUBARITHMETICCIRCUIT_1300_440 (
    .SUB_ACTIVATED(RESULT_ACTIVE), .LEFT(ACC_VALUE), .RIGHT(multiplexer_1_out),
    .INPUT_VALID(ACC_SUB_VALID_out), .RESULT(RESULT), .OVERFLOW(OVERFLOW), .RESULT_VALID(RESULT_VALID));

  // Notes on the sheet:
  //   MEMORY_VALID →
  //   SUB_VALID →
  //   CONST_VALID →
endmodule

module MulSubCircuit (
  input  MUL_CONST,
  input  MUL_ADDRESS,
  input  MUL_ADDRESS_REGISTER,
  input  MUL_ADDRESS_REGISTER_PLUS_OFFSET,
  input  [7:0] ACC_VALUE,
  input  [7:0] MEMORY_VALUE,
  input  [7:0] IMMEDIATE_VALUE,
  input  MEMORY_VALID,
  input  ACC_VALID,
  output [7:0] RESULT,
  output OVERFLOW,
  output RESULT_VALID,
  output RESULT_ACTIVE
);

  wire ACC_MUL_VALID_out, multiplexer_2_out;
  wire [7:0] multiplexer_1_out;

  or ACC_MUL_MEMORY_SELECT (RESULT_ACTIVE, MUL_CONST, MUL_ADDRESS, MUL_ADDRESS_REGISTER, MUL_ADDRESS_REGISTER_PLUS_OFFSET);
  Multiplexer #(.width(8)) multiplexer_1 (
    .in0(MEMORY_VALUE), .in1(IMMEDIATE_VALUE), .out(multiplexer_1_out), .sel(MUL_CONST));
  Multiplexer multiplexer_2 (.in0(1'b1), .in1(MEMORY_VALID), .out(multiplexer_2_out), .sel(MUL_CONST));
  and ACC_MUL_VALID (ACC_MUL_VALID_out, multiplexer_2_out, ACC_VALID);
  MulArithmeticCircuit MULARITHMETICCIRCUIT_1300_440 (
    .MUL_ACTIVATED(RESULT_ACTIVE), .LEFT(ACC_VALUE), .RIGHT(multiplexer_1_out),
    .INPUT_VALID(ACC_MUL_VALID_out), .RESULT(RESULT), .OVERFLOW(OVERFLOW), .RESULT_VALID(RESULT_VALID));

  // Notes on the sheet:
  //   MEMORY_VALID →
  //   MUL_VALID →
  //   CONST_VALID →
endmodule

module MulArithmeticCircuit (
  input  MUL_ACTIVATED,
  input  [7:0] LEFT,
  input  [7:0] RIGHT,
  input  INPUT_VALID,
  output [7:0] RESULT,
  output OVERFLOW,
  output RESULT_VALID
);

  wire NO_OVERFLOW_out, OPERAND_SIGN_DIFFERENT_out, RESULT_SIGN_CHANGED_out;
  wire [6:0] multiplexer_2_out;
  wire [7:0] multiplexer_1_out;
  wire [7:7] multiplexer_2_out_2;

  Multiplexer #(.width(8)) multiplexer_1 (.in0({8{1'b0}}), .in1(LEFT), .out(multiplexer_1_out), .sel(MUL_ACTIVATED));
  Multiplexer #(.width(8)) multiplexer_2 (
    .in0({8{1'b0}}), .in1(RIGHT), .out({multiplexer_2_out_2[7], multiplexer_2_out}), .sel(MUL_ACTIVATED));
  Multiplier multiplier_1 (
    .a(multiplexer_1_out), .b({multiplexer_2_out_2[7], multiplexer_2_out}), .out(RESULT));  // open: cin, cout
  xor OPERAND_SIGN_DIFFERENT (OPERAND_SIGN_DIFFERENT_out, multiplexer_1_out[7], multiplexer_2_out_2[7]);
  xor RESULT_SIGN_CHANGED (RESULT_SIGN_CHANGED_out, RESULT[7], multiplexer_1_out[7]);
  not NO_OVERFLOW (NO_OVERFLOW_out, OPERAND_SIGN_DIFFERENT_out);
  and SIGN_OVERFLOW (OVERFLOW, RESULT_SIGN_CHANGED_out, OPERAND_SIGN_DIFFERENT_out);
  and RANGE_VALID (RESULT_VALID, NO_OVERFLOW_out, INPUT_VALID);

  // Notes on the sheet:
  //   signed MUL: overflow = (left_sign XOR right_sign) AND (left_sign XOR result_sign)
endmodule

module DivSubCircuit (
  input  DIV_CONST,
  input  DIV_ADDRESS,
  input  DIV_ADDRESS_REGISTER,
  input  DIV_ADDRESS_REGISTER_PLUS_OFFSET,
  input  [7:0] ACC_VALUE,
  input  [7:0] MEMORY_VALUE,
  input  [7:0] IMMEDIATE_VALUE,
  input  MEMORY_VALID,
  input  ACC_VALID,
  output [7:0] RESULT,
  output RESULT_VALID,
  output DIVIDE_BY_ZERO,
  output RESULT_ACTIVE
);

  wire ACC_DIV_VALID_out, multiplexer_2_out;
  wire [7:0] multiplexer_1_out;

  or ACC_DIV_MEMORY_SELECT (RESULT_ACTIVE, DIV_CONST, DIV_ADDRESS, DIV_ADDRESS_REGISTER, DIV_ADDRESS_REGISTER_PLUS_OFFSET);
  Multiplexer #(.width(8)) multiplexer_1 (
    .in0(MEMORY_VALUE), .in1(IMMEDIATE_VALUE), .out(multiplexer_1_out), .sel(DIV_CONST));
  Multiplexer multiplexer_2 (.in0(1'b1), .in1(MEMORY_VALID), .out(multiplexer_2_out), .sel(DIV_CONST));
  and ACC_DIV_VALID (ACC_DIV_VALID_out, multiplexer_2_out, ACC_VALID);
  DivArithmeticCircuit DIVARITHMETICCIRCUIT_1300_440 (
    .DIV_ACTIVATED(RESULT_ACTIVE), .LEFT(ACC_VALUE), .RIGHT(multiplexer_1_out),
    .INPUT_VALID(ACC_DIV_VALID_out), .RESULT(RESULT), .RESULT_VALID(RESULT_VALID),
    .DIVIDE_BY_ZERO(DIVIDE_BY_ZERO));

  // Notes on the sheet:
  //   MEMORY_VALID →
  //   DIV_VALID →
  //   CONST_VALID →
endmodule

module DivArithmeticCircuit (
  input  DIV_ACTIVATED,
  input  [7:0] LEFT,
  input  [7:0] RIGHT,
  input  INPUT_VALID,
  output [7:0] RESULT,
  output RESULT_VALID,
  output DIVIDE_BY_ZERO
);
endmodule

module AddArithmeticCircuit (
  input  ADD_ACTIVATED,
  input  [7:0] LEFT,
  input  [7:0] RIGHT,
  input  INPUT_VALID,
  output [7:0] RESULT,
  output OVERFLOW,
  output RESULT_VALID
);

  wire NO_OVERFLOW_out, OPERAND_SIGN_DIFFERENT_out, OPERAND_SIGN_SAME_out, RESULT_SIGN_CHANGED_out;
  wire [6:0] multiplexer_2_out;
  wire [7:0] multiplexer_1_out;
  wire [7:7] multiplexer_2_out_2;

  Multiplexer #(.width(8)) multiplexer_1 (.in0({8{1'b0}}), .in1(LEFT), .out(multiplexer_1_out), .sel(ADD_ACTIVATED));
  Multiplexer #(.width(8)) multiplexer_2 (
    .in0({8{1'b0}}), .in1(RIGHT), .out({multiplexer_2_out_2[7], multiplexer_2_out}), .sel(ADD_ACTIVATED));
  Adder adder_1 (
    .a(multiplexer_1_out), .b({multiplexer_2_out_2[7], multiplexer_2_out}), .out(RESULT));  // open: cin, cout
  xor OPERAND_SIGN_DIFFERENT (OPERAND_SIGN_DIFFERENT_out, multiplexer_1_out[7], multiplexer_2_out_2[7]);
  not OPERAND_SIGN_SAME (OPERAND_SIGN_SAME_out, OPERAND_SIGN_DIFFERENT_out);
  xor RESULT_SIGN_CHANGED (RESULT_SIGN_CHANGED_out, RESULT[7], multiplexer_1_out[7]);
  not NO_OVERFLOW (NO_OVERFLOW_out, OPERAND_SIGN_SAME_out);
  and SIGN_OVERFLOW (OVERFLOW, RESULT_SIGN_CHANGED_out, OPERAND_SIGN_SAME_out);
  and RANGE_VALID (RESULT_VALID, NO_OVERFLOW_out, INPUT_VALID);

  // Notes on the sheet:
  //   signed ADD: overflow = NOT(left_sign XOR right_sign) AND (left_sign XOR result_sign)
endmodule

module SubArithmeticCircuit (
  input  SUB_ACTIVATED,
  input  [7:0] LEFT,
  input  [7:0] RIGHT,
  input  INPUT_VALID,
  output [7:0] RESULT,
  output OVERFLOW,
  output RESULT_VALID
);

  wire NO_OVERFLOW_out, OPERAND_SIGN_DIFFERENT_out, RESULT_SIGN_CHANGED_out;
  wire [6:0] multiplexer_2_out;
  wire [7:0] multiplexer_1_out;
  wire [7:7] multiplexer_2_out_2;

  Multiplexer #(.width(8)) multiplexer_1 (.in0({8{1'b0}}), .in1(LEFT), .out(multiplexer_1_out), .sel(SUB_ACTIVATED));
  Multiplexer #(.width(8)) multiplexer_2 (
    .in0({8{1'b0}}), .in1(RIGHT), .out({multiplexer_2_out_2[7], multiplexer_2_out}), .sel(SUB_ACTIVATED));
  Subtractor subtractor_1 (
    .a(multiplexer_1_out), .b({multiplexer_2_out_2[7], multiplexer_2_out}), .out(RESULT));  // open: bin, bout
  xor OPERAND_SIGN_DIFFERENT (OPERAND_SIGN_DIFFERENT_out, multiplexer_1_out[7], multiplexer_2_out_2[7]);
  xor RESULT_SIGN_CHANGED (RESULT_SIGN_CHANGED_out, RESULT[7], multiplexer_1_out[7]);
  not NO_OVERFLOW (NO_OVERFLOW_out, OPERAND_SIGN_DIFFERENT_out);
  and SIGN_OVERFLOW (OVERFLOW, RESULT_SIGN_CHANGED_out, OPERAND_SIGN_DIFFERENT_out);
  and RANGE_VALID (RESULT_VALID, NO_OVERFLOW_out, INPUT_VALID);

  // Notes on the sheet:
  //   signed SUB: overflow = (left_sign XOR right_sign) AND (left_sign XOR result_sign)
endmodule

module AddressRangeFBox (
  input  OFFSET_CARRY,
  input  EFFECTIVE_REGISTER_MODE,
  input  EFFECTIVE_OFFSET_MODE,
  input  ADDRESS_OUT_OF_RANGE,
  input  LOAD_ADDRESS,
  input  ADD_ADDRESS,
  input  SUB_ADDRESS,
  input  MUL_ADDRESS,
  input  DIV_ADDRESS,
  input  AND_ADDRESS,
  input  OR_ADDRESS,
  input  STORE_ADDRESS,
  output ACTIVE_ADDRESS_OUT_OF_RANGE
);

  wire ACTIVE_ADDRESS_RANGE_GATE_out, ACTIVE_OFFSET_ADDRESS_ERROR_out, DIRECT_MEMORY_ADDRESS_ACTIVE_out,
       MEMORY_ADDRESS_ACTIVE_out;

  or DIRECT_MEMORY_ADDRESS_ACTIVE (DIRECT_MEMORY_ADDRESS_ACTIVE_out, LOAD_ADDRESS, ADD_ADDRESS, SUB_ADDRESS, MUL_ADDRESS, DIV_ADDRESS, AND_ADDRESS, OR_ADDRESS, STORE_ADDRESS);
  or MEMORY_ADDRESS_ACTIVE (MEMORY_ADDRESS_ACTIVE_out, DIRECT_MEMORY_ADDRESS_ACTIVE_out, EFFECTIVE_REGISTER_MODE, EFFECTIVE_OFFSET_MODE);
  and ACTIVE_ADDRESS_RANGE_GATE (ACTIVE_ADDRESS_RANGE_GATE_out, MEMORY_ADDRESS_ACTIVE_out, ADDRESS_OUT_OF_RANGE);
  and ACTIVE_OFFSET_ADDRESS_ERROR (ACTIVE_OFFSET_ADDRESS_ERROR_out, OFFSET_CARRY, EFFECTIVE_OFFSET_MODE);
  or ACTIVE_ADDRESS_ERROR (ACTIVE_ADDRESS_OUT_OF_RANGE, ACTIVE_OFFSET_ADDRESS_ERROR_out, ACTIVE_ADDRESS_RANGE_GATE_out);
endmodule

module OrArithmeticCircuit (
  input  OR_ACTIVATED,
  input  [7:0] LEFT,
  input  [7:0] RIGHT,
  input  INPUT_VALID,
  output [7:0] RESULT,
  output RESULT_VALID
);

  wire [7:0] BITWISE_OR_out;

  assign BITWISE_OR_out = LEFT | RIGHT;  // OR_Gate BITWISE_OR, 8 bits wide
  Multiplexer #(.width(8)) multiplexer_1 (.in0({8{1'b0}}), .in1(BITWISE_OR_out), .out(RESULT), .sel(OR_ACTIVATED));
  and ACTIVE_OR_VALID (RESULT_VALID, OR_ACTIVATED, INPUT_VALID);

  // Notes on the sheet:
  //   bitwise OR: inactive outputs are neutral
endmodule

module OrSubCircuit (
  input  OR_CONST,
  input  OR_ADDRESS,
  input  OR_ADDRESS_REGISTER,
  input  OR_ADDRESS_REGISTER_PLUS_OFFSET,
  input  [7:0] ACC_VALUE,
  input  [7:0] MEMORY_VALUE,
  input  [7:0] IMMEDIATE_VALUE,
  input  MEMORY_VALID,
  input  ACC_VALID,
  output [7:0] RESULT,
  output RESULT_VALID,
  output RESULT_ACTIVE
);

  wire ACC_OR_VALID_out, multiplexer_2_out;
  wire [7:0] multiplexer_1_out;

  or ACC_OR_MEMORY_SELECT (RESULT_ACTIVE, OR_CONST, OR_ADDRESS, OR_ADDRESS_REGISTER, OR_ADDRESS_REGISTER_PLUS_OFFSET);
  Multiplexer #(.width(8)) multiplexer_1 (
    .in0(MEMORY_VALUE), .in1(IMMEDIATE_VALUE), .out(multiplexer_1_out), .sel(OR_CONST));
  Multiplexer multiplexer_2 (.in0(1'b1), .in1(MEMORY_VALID), .out(multiplexer_2_out), .sel(OR_CONST));
  and ACC_OR_VALID (ACC_OR_VALID_out, multiplexer_2_out, ACC_VALID);
  OrArithmeticCircuit ORARITHMETICCIRCUIT_1300_440 (
    .OR_ACTIVATED(RESULT_ACTIVE), .LEFT(ACC_VALUE), .RIGHT(multiplexer_1_out),
    .INPUT_VALID(ACC_OR_VALID_out), .RESULT(RESULT), .RESULT_VALID(RESULT_VALID));

  // Notes on the sheet:
  //   MEMORY_VALID →
  //   OR_VALID →
  //   CONST_VALID →
endmodule

module XorArithmeticCircuit (
  input  XOR_ACTIVATED,
  input  [7:0] LEFT,
  input  [7:0] RIGHT,
  input  INPUT_VALID,
  output [7:0] RESULT,
  output RESULT_VALID
);

  wire [7:0] BITWISE_XOR_out;

  assign BITWISE_XOR_out = LEFT ^ RIGHT;  // XOR_Gate BITWISE_XOR, 8 bits wide
  Multiplexer #(.width(8)) multiplexer_1 (.in0({8{1'b0}}), .in1(BITWISE_XOR_out), .out(RESULT), .sel(XOR_ACTIVATED));
  and ACTIVE_XOR_VALID (RESULT_VALID, XOR_ACTIVATED, INPUT_VALID);

  // Notes on the sheet:
  //   bitwise XOR: inactive outputs are neutral
endmodule

module XorSubCircuit (
  input  XOR_CONST,
  input  XOR_ADDRESS,
  input  XOR_ADDRESS_REGISTER,
  input  XOR_ADDRESS_REGISTER_PLUS_OFFSET,
  input  [7:0] ACC_VALUE,
  input  [7:0] MEMORY_VALUE,
  input  [7:0] IMMEDIATE_VALUE,
  input  MEMORY_VALID,
  input  ACC_VALID,
  output [7:0] RESULT,
  output RESULT_VALID,
  output RESULT_ACTIVE
);

  wire ACC_XOR_VALID_out, multiplexer_2_out;
  wire [7:0] multiplexer_1_out;

  or ACC_XOR_MEMORY_SELECT (RESULT_ACTIVE, XOR_CONST, XOR_ADDRESS, XOR_ADDRESS_REGISTER, XOR_ADDRESS_REGISTER_PLUS_OFFSET);
  Multiplexer #(.width(8)) multiplexer_1 (
    .in0(MEMORY_VALUE), .in1(IMMEDIATE_VALUE), .out(multiplexer_1_out), .sel(XOR_CONST));
  Multiplexer multiplexer_2 (.in0(1'b1), .in1(MEMORY_VALID), .out(multiplexer_2_out), .sel(XOR_CONST));
  and ACC_XOR_VALID (ACC_XOR_VALID_out, multiplexer_2_out, ACC_VALID);
  XorArithmeticCircuit ORARITHMETICCIRCUIT_1300_440 (
    .XOR_ACTIVATED(RESULT_ACTIVE), .LEFT(ACC_VALUE), .RIGHT(multiplexer_1_out),
    .INPUT_VALID(ACC_XOR_VALID_out), .RESULT(RESULT), .RESULT_VALID(RESULT_VALID));

  // Notes on the sheet:
  //   MEMORY_VALID →
  //   XOR_VALID →
  //   CONST_VALID →
endmodule

module JumpBox (
  input  ERROR_OVF,
  input  ERROR_DIV0,
  input  ERROR_ADDR,
  input  ERROR_INV,
  input  ERROR_ILL,
  input  ERROR_INPUT,
  input  JUMP_ADR,
  input  JUMP_ZERO,
  input  JUMP_NOT_ZERO,
  input  JUMP_NEGATIVE,
  input  JUMP_ERROR,
  input  JUMP_NOT_ERROR,
  input  NEGATIVE,
  input  ZERO,
  output IS_NOT_ZERO,
  output DEC_JUMP_NOT_ZERO
);

  wire ANY_ERROR_FOR_JUMP_out, INVERT_ANY_ERROR_FOR_JUMP_NOT_ERROR_out, JUMP_ADR_OR_JNZ_CONTROL_out,
       JUMP_ADR_OR_NOT_ZERO_out, JUMP_ERROR_AND_ANY_ERROR_out, JUMP_ERROR_OR_PREVIOUS_CONTROLS_out,
       JUMP_ERROR_OR_PREVIOUS_TAKEN_out, JUMP_NEGATIVE_AND_NEGATIVE_out,
       JUMP_NEGATIVE_OR_PREVIOUS_CONTROLS_out, JUMP_NEGATIVE_OR_PREVIOUS_TAKEN_out,
       JUMP_NOT_ERROR_AND_NO_ERROR_out, JUMP_ZERO_AND_ZERO_out, JUMP_ZERO_OR_PREVIOUS_CONTROLS_out,
       JUMP_ZERO_OR_PREVIOUS_TAKEN_out;

  or ANY_ERROR_FOR_JUMP (ANY_ERROR_FOR_JUMP_out, ERROR_DIV0, ERROR_ADDR, ERROR_INV, ERROR_ILL);
  or JUMP_ADR_OR_JNZ_CONTROL (JUMP_ADR_OR_JNZ_CONTROL_out, JUMP_NOT_ZERO, JUMP_ADR);
  not INVERT_ZERO_FOR_JNZ (ZERO, ZERO);
  or JUMP_ZERO_OR_PREVIOUS_CONTROLS (JUMP_ZERO_OR_PREVIOUS_CONTROLS_out, JUMP_ADR_OR_JNZ_CONTROL_out, JUMP_ZERO);
  or JUMP_ADR_OR_NOT_ZERO (JUMP_ADR_OR_NOT_ZERO_out, JUMP_ADR, ZERO);
  and JUMP_ZERO_AND_ZERO (JUMP_ZERO_AND_ZERO_out, JUMP_ZERO, ZERO);
  and JUMP_NEGATIVE_AND_NEGATIVE (JUMP_NEGATIVE_AND_NEGATIVE_out, JUMP_NEGATIVE, NEGATIVE);
  or JUMP_NEGATIVE_OR_PREVIOUS_CONTROLS (JUMP_NEGATIVE_OR_PREVIOUS_CONTROLS_out, JUMP_ZERO_OR_PREVIOUS_CONTROLS_out, JUMP_NEGATIVE);
  or JUMP_ZERO_OR_PREVIOUS_TAKEN (JUMP_ZERO_OR_PREVIOUS_TAKEN_out, JUMP_ADR_OR_NOT_ZERO_out, JUMP_ZERO_AND_ZERO_out);
  or JUMP_NEGATIVE_OR_PREVIOUS_TAKEN (JUMP_NEGATIVE_OR_PREVIOUS_TAKEN_out, JUMP_ZERO_OR_PREVIOUS_TAKEN_out, JUMP_NEGATIVE_AND_NEGATIVE_out);
  and JUMP_ERROR_AND_ANY_ERROR (JUMP_ERROR_AND_ANY_ERROR_out, JUMP_NOT_ERROR, ANY_ERROR_FOR_JUMP_out);
  not INVERT_ANY_ERROR_FOR_JUMP_NOT_ERROR (INVERT_ANY_ERROR_FOR_JUMP_NOT_ERROR_out, ANY_ERROR_FOR_JUMP_out);
  or JUMP_ERROR_OR_PREVIOUS_CONTROLS (JUMP_ERROR_OR_PREVIOUS_CONTROLS_out, JUMP_NOT_ERROR, JUMP_NEGATIVE_OR_PREVIOUS_CONTROLS_out);
  or JUMP_ERROR_OR_PREVIOUS_TAKEN (JUMP_ERROR_OR_PREVIOUS_TAKEN_out, JUMP_NEGATIVE_OR_PREVIOUS_TAKEN_out, JUMP_ERROR_AND_ANY_ERROR_out);
  and JUMP_NOT_ERROR_AND_NO_ERROR (JUMP_NOT_ERROR_AND_NO_ERROR_out, JUMP_ERROR, INVERT_ANY_ERROR_FOR_JUMP_NOT_ERROR_out);
  or JUMP_NOT_ERROR_OR_PREVIOUS_CONTROLS (IS_NOT_ZERO, JUMP_ERROR_OR_PREVIOUS_CONTROLS_out, JUMP_ERROR);
  or JUMP_NOT_ERROR_OR_PREVIOUS_TAKEN (DEC_JUMP_NOT_ZERO, JUMP_ERROR_OR_PREVIOUS_TAKEN_out, JUMP_NOT_ERROR_AND_NO_ERROR_out);
endmodule
