// Logisim project TinyCPU.circ as structural Verilog: 21 circuits, main circuit TinyCPUMain
module TinyCPUMain (
  input  CLK,
  input  RESET,
  output [15:0] PRINT_VALUE,
  output PRINT_ADDRESS_VALID,
  output [15:0] PRINT_ADDRESS_VALUE,
  output PRINT_VALID,
  output ERROR_OVF,
  output ERROR_DIV0,
  output ERROR_ADDR,
  output ERROR_INV,
  output ERROR_ILL,
  output ERROR_INPUT,
  output PRINT_ENABLE,
  output PRINT_ADDRESS_ENABLE,
  output HALTED,
  output HALTED_WITH_ERROR
);

  wire ADDRESS_PATH_address_valid, ADDRESS_PATH_offset_carry, ADDRESS_RANGE_FBOX_active_address_out_of_range,
       DATAPATH_INSTANCE_negative, DATAPATH_INSTANCE_zero, EFFECTIVE_ADDRESS_FBOX_address_out_of_range,
       EFFECTIVE_ADDRESS_FBOX_effective_offset_mode, EFFECTIVE_ADDRESS_FBOX_effective_register_mode,
       FETCH_DECODE_CONTROLS_add_operand, FETCH_DECODE_CONTROLS_addr_argument,
       FETCH_DECODE_CONTROLS_addr_reg_argument, FETCH_DECODE_CONTROLS_addr_reg_offs_argument,
       FETCH_DECODE_CONTROLS_and_operand, FETCH_DECODE_CONTROLS_const_argument,
       FETCH_DECODE_CONTROLS_div_operand, FETCH_DECODE_CONTROLS_input, FETCH_DECODE_CONTROLS_jump_adr,
       FETCH_DECODE_CONTROLS_jump_error, FETCH_DECODE_CONTROLS_jump_negative,
       FETCH_DECODE_CONTROLS_jump_not_error, FETCH_DECODE_CONTROLS_jump_not_zero,
       FETCH_DECODE_CONTROLS_jump_zero, FETCH_DECODE_CONTROLS_mul_operand, FETCH_DECODE_CONTROLS_not,
       FETCH_DECODE_CONTROLS_or_operand, FETCH_DECODE_CONTROLS_set_addr, FETCH_DECODE_CONTROLS_set_div0,
       FETCH_DECODE_CONTROLS_set_inv, FETCH_DECODE_CONTROLS_sub_operand, FETCH_DECODE_CONTROLS_xor_operand,
       FETCH_DECODE_halt_error, FETCH_DECODE_jump_not_zero, JUMP_BOX_dec_jump_not_zero, JUMP_BOX_is_not_zero,
       MEMORY_WRITE_REQUEST_out, OPERATIONS_INSTANCE_divide_by_zero, OPERATIONS_INSTANCE_invalid_operand,
       OPERATIONS_INSTANCE_overflow, OPERATIONS_INSTANCE_result_is_valid, undriven, undriven_2, undriven_3;
  wire [11:0] FETCH_DECODE_pc_out;
  wire [15:0] ADDRESS_PATH_address, ADDRESS_PATH_address_plus_offset,
       EFFECTIVE_ADDRESS_FBOX_effective_memory_address,
       EFFECTIVE_ADDRESS_FBOX_effective_register_selected_out, multiplexer_1_out,
       OPERATIONS_INSTANCE_result_value;
  wire [21:0] FETCH_DECODE_opcode;

  or MEMORY_WRITE_REQUEST (MEMORY_WRITE_REQUEST_out, PRINT_ADDRESS_ENABLE, PRINT_ENABLE, HALTED);
  FetchDecode FETCH_DECODE (
    .CLK(CLK), .RESET(RESET), .DEC_JUMP_NOT_ZERO(JUMP_BOX_is_not_zero),
    .NOT_ZERO(JUMP_BOX_dec_jump_not_zero), .PROGRAM_LIMIT(16'hfff), .DEC_HALT_ERROR(1'b1),
    .JUMP_NOT_ZERO(FETCH_DECODE_jump_not_zero), .HALT_ERROR(FETCH_DECODE_halt_error),
    .PC_OUT(FETCH_DECODE_pc_out), .OPCODE(FETCH_DECODE_opcode));
  Memory MEMORY_INSTANCE (
    .ADDRESS(EFFECTIVE_ADDRESS_FBOX_effective_memory_address), .WRITE_ENABLE(MEMORY_WRITE_REQUEST_out),
    .CLK(CLK), .VALID_IN(PRINT_VALID), .DATA_IN(PRINT_VALUE), .MEMORY_VALID(PRINT_ADDRESS_VALID),
    .MEMORY_DATA(PRINT_ADDRESS_VALUE));
  // Probe on FETCH_DECODE_jump_not_zero
  // Probe on FETCH_DECODE_halt_error
  // Probe on FETCH_DECODE_pc_out
  AddressPath ADDRESS_PATH (
    .ADDRESS_IN(16'h1), .AR_LOAD(undriven), .OFFSET(16'h1), .VALID_IN(1'b1), .CLK(CLK),
    .ADDRESS_PATH_STARTUP_RESET(1'b1), .ADDRESS(ADDRESS_PATH_address),
    .ADDRESS_PLUS_OFFSET(ADDRESS_PATH_address_plus_offset), .OFFSET_CARRY(ADDRESS_PATH_offset_carry),
    .ADDRESS_VALID(ADDRESS_PATH_address_valid));
  FetchDecodeControls FETCH_DECODE_CONTROLS (
    .OPCODE(FETCH_DECODE_opcode[21:16]), .ADD_OPERAND(FETCH_DECODE_CONTROLS_add_operand),
    .SUB_OPERAND(FETCH_DECODE_CONTROLS_sub_operand), .MUL_OPERAND(FETCH_DECODE_CONTROLS_mul_operand),
    .DIV_OPERAND(FETCH_DECODE_CONTROLS_div_operand), .AND_OPERAND(FETCH_DECODE_CONTROLS_and_operand),
    .OR_OPERAND(FETCH_DECODE_CONTROLS_or_operand), .XOR_OPERAND(FETCH_DECODE_CONTROLS_xor_operand),
    .CONST_ARGUMENT(FETCH_DECODE_CONTROLS_const_argument),
    .ADDR_ARGUMENT(FETCH_DECODE_CONTROLS_addr_argument),
    .ADDR_REG_ARGUMENT(FETCH_DECODE_CONTROLS_addr_reg_argument),
    .ADDR_REG_OFFS_ARGUMENT(FETCH_DECODE_CONTROLS_addr_reg_offs_argument), .NOT(FETCH_DECODE_CONTROLS_not),
    .JUMP_ADR(FETCH_DECODE_CONTROLS_jump_adr), .JUMP_ZERO(FETCH_DECODE_CONTROLS_jump_zero),
    .JUMP_NOT_ZERO(FETCH_DECODE_CONTROLS_jump_not_zero), .JUMP_NEGATIVE(FETCH_DECODE_CONTROLS_jump_negative),
    .JUMP_ERROR(FETCH_DECODE_CONTROLS_jump_error), .JUMP_NOT_ERROR(FETCH_DECODE_CONTROLS_jump_not_error),
    .SET_DIV0(FETCH_DECODE_CONTROLS_set_div0), .SET_ADDR(FETCH_DECODE_CONTROLS_set_addr),
    .SET_INV(FETCH_DECODE_CONTROLS_set_inv), .INPUT(FETCH_DECODE_CONTROLS_input), .PRINT(PRINT_ENABLE),
    .PRINT_ADR(PRINT_ADDRESS_ENABLE), .HALT(HALTED), .HALT_ERROR(HALTED_WITH_ERROR));  // open: LOAD_OPERAND, STORE_OPERAND, SET_OVF, SET_ILL, SET_INPUT, CLEAR_ERROR, INVALID_OPERAND
  // Probe on FETCH_DECODE_CONTROLS_jump_adr
  // Probe on FETCH_DECODE_CONTROLS_jump_zero
  // Probe on FETCH_DECODE_CONTROLS_jump_negative
  // Probe on FETCH_DECODE_CONTROLS_jump_error
  // Probe on FETCH_DECODE_CONTROLS_jump_not_error
  // Probe on FETCH_DECODE_CONTROLS_set_div0
  // Probe on FETCH_DECODE_CONTROLS_set_addr
  // Probe on FETCH_DECODE_CONTROLS_set_inv
  // Probe on FETCH_DECODE_CONTROLS_input
  Datapath DATAPATH_INSTANCE (
    .DATA_IN(OPERATIONS_INSTANCE_result_value), .DATAPATH_STARTUP_RESET(1'b0), .ACC_LOAD(undriven),
    .VALID_IN(OPERATIONS_INSTANCE_overflow), .CLK(CLK), .ACC_OUT(PRINT_VALUE), .ZERO(DATAPATH_INSTANCE_zero),
    .NEGATIVE(DATAPATH_INSTANCE_negative), .ACC_VALID_OUT(PRINT_VALID));
  Multiplexer #(.width(16)) multiplexer_1 (
    .in0(FETCH_DECODE_opcode[15:0]), .in1(PRINT_ADDRESS_VALUE), .out(multiplexer_1_out), .sel(undriven_2));
  ErrorFlags ERROR_FLAGS (
    .CLK(CLK), .SET_OVF(OPERATIONS_INSTANCE_overflow), .SET_DIV0(OPERATIONS_INSTANCE_divide_by_zero),
    .SET_ADDR(ADDRESS_RANGE_FBOX_active_address_out_of_range), .SET_INV(OPERATIONS_INSTANCE_invalid_operand),
    .OVF_OUT(ERROR_OVF), .DIV0_OUT(ERROR_DIV0), .ADDR_OUT(ERROR_ADDR), .INV_OUT(ERROR_INV),
    .ILL_OUT(ERROR_ILL), .INPUT_OUT(ERROR_INPUT));  // open: CLEAR_ERROR, SET_ILL, SET_INPUT
  Operations OPERATIONS_INSTANCE (
    .ACC_VALUE(PRINT_VALUE), .MEMORY_VALUE(multiplexer_1_out), .IMMEDIATE_VALUE(PRINT_ADDRESS_VALUE),
    .MEMORY_VALID(PRINT_ADDRESS_VALID), .ACC_VALID(PRINT_VALID),
    .CONST_OPERAND(FETCH_DECODE_CONTROLS_const_argument), .ADD_OPERAND(FETCH_DECODE_CONTROLS_add_operand),
    .SUB_OPERAND(FETCH_DECODE_CONTROLS_sub_operand), .MUL_OPERAND(FETCH_DECODE_CONTROLS_mul_operand),
    .DIV_OPERAND(FETCH_DECODE_CONTROLS_div_operand), .AND_OPERAND(FETCH_DECODE_CONTROLS_and_operand),
    .OR_OPERAND(FETCH_DECODE_CONTROLS_or_operand), .XOR_OPERAND(FETCH_DECODE_CONTROLS_xor_operand),
    .NOT_OPERAND(FETCH_DECODE_CONTROLS_not), .RESULT_VALUE(OPERATIONS_INSTANCE_result_value),
    .OVERFLOW(OPERATIONS_INSTANCE_overflow), .RESULT_IS_VALID(OPERATIONS_INSTANCE_result_is_valid),
    .INVALID_OPERAND(OPERATIONS_INSTANCE_invalid_operand), .DIVIDE_BY_ZERO(OPERATIONS_INSTANCE_divide_by_zero));
  EffectiveAddress EFFECTIVE_ADDRESS_FBOX (
    .DIRECT_ADDR(FETCH_DECODE_opcode[15:0]), .REG_ADDR(ADDRESS_PATH_address),
    .ADDR_REG_ARGUMENT(FETCH_DECODE_CONTROLS_addr_argument),
    .OFFSET_ADDR(EFFECTIVE_ADDRESS_FBOX_effective_register_selected_out),
    .REG_SELECTED(ADDRESS_PATH_address_plus_offset),
    .ADDR_REG_OFFS_ARGUMENT(FETCH_DECODE_CONTROLS_addr_reg_offs_argument),
    .EFFECTIVE_REGISTER_SELECTED_OUT(EFFECTIVE_ADDRESS_FBOX_effective_register_selected_out),
    .EFFECTIVE_REGISTER_MODE(EFFECTIVE_ADDRESS_FBOX_effective_register_mode),
    .EFFECTIVE_MEMORY_ADDRESS(EFFECTIVE_ADDRESS_FBOX_effective_memory_address),
    .EFFECTIVE_OFFSET_MODE(EFFECTIVE_ADDRESS_FBOX_effective_offset_mode),
    .ADDRESS_OUT_OF_RANGE(EFFECTIVE_ADDRESS_FBOX_address_out_of_range));
  AddressRangeFBox ADDRESS_RANGE_FBOX (
    .OFFSET_CARRY(ADDRESS_PATH_offset_carry),
    .EFFECTIVE_REGISTER_MODE(EFFECTIVE_ADDRESS_FBOX_effective_register_mode),
    .EFFECTIVE_OFFSET_MODE(EFFECTIVE_ADDRESS_FBOX_effective_offset_mode),
    .ADDRESS_OUT_OF_RANGE(EFFECTIVE_ADDRESS_FBOX_address_out_of_range),
    .ADDRESS_OPERAND(FETCH_DECODE_CONTROLS_addr_reg_argument),
    .ACTIVE_ADDRESS_OUT_OF_RANGE(ADDRESS_RANGE_FBOX_active_address_out_of_range));
  // Probe on ADDRESS_PATH_address_valid
  // Probe on undriven_2
  // Probe on undriven_3
  // Probe on nothing
  // Probe on OPERATIONS_INSTANCE_result_is_valid
  // Probe on EFFECTIVE_ADDRESS_FBOX_effective_register_selected_out
  // Probe on EFFECTIVE_ADDRESS_FBOX_effective_memory_address
  JumpBox JUMP_BOX (
    .ERROR_OVF(ERROR_OVF), .ERROR_DIV0(ERROR_DIV0), .ERROR_ADDR(ERROR_ADDR), .ERROR_INV(ERROR_INV),
    .ERROR_ILL(ERROR_ILL), .ERROR_INPUT(ERROR_INPUT), .JUMP_ADR(FETCH_DECODE_CONTROLS_jump_adr),
    .JUMP_ZERO(FETCH_DECODE_CONTROLS_jump_zero), .JUMP_NOT_ZERO(FETCH_DECODE_CONTROLS_jump_not_zero),
    .JUMP_NEGATIVE(FETCH_DECODE_CONTROLS_jump_negative), .JUMP_ERROR(FETCH_DECODE_CONTROLS_jump_error),
    .JUMP_NOT_ERROR(FETCH_DECODE_CONTROLS_jump_not_error), .NEGATIVE(DATAPATH_INSTANCE_negative),
    .ZERO(DATAPATH_INSTANCE_zero), .IS_NOT_ZERO(JUMP_BOX_is_not_zero),
    .DEC_JUMP_NOT_ZERO(JUMP_BOX_dec_jump_not_zero));
endmodule

module EffectiveAddress (
  input  [15:0] DIRECT_ADDR,
  input  [15:0] REG_ADDR,
  input  ADDR_REG_ARGUMENT,
  input  [15:0] OFFSET_ADDR,
  input  [15:0] REG_SELECTED,
  input  ADDR_REG_OFFS_ARGUMENT,
  output [15:0] EFFECTIVE_REGISTER_SELECTED_OUT,
  output EFFECTIVE_REGISTER_MODE,
  output [15:0] EFFECTIVE_MEMORY_ADDRESS,
  output EFFECTIVE_OFFSET_MODE,
  output ADDRESS_OUT_OF_RANGE
);

  Multiplexer #(.width(16)) multiplexer_1 (
    .in0(DIRECT_ADDR), .in1(REG_ADDR), .out(EFFECTIVE_REGISTER_SELECTED_OUT), .sel(ADDR_REG_ARGUMENT));
  Multiplexer #(.width(16)) multiplexer_2 (
    .in0(REG_SELECTED), .in1(OFFSET_ADDR), .out(EFFECTIVE_MEMORY_ADDRESS), .sel(ADDR_REG_OFFS_ARGUMENT));
  Comparator #(.width(16)) comparator_1 (
    .a(EFFECTIVE_MEMORY_ADDRESS), .b(16'hfff), .gt(ADDRESS_OUT_OF_RANGE));  // open: eq, lt

  assign EFFECTIVE_OFFSET_MODE = ADDR_REG_OFFS_ARGUMENT;
  assign EFFECTIVE_REGISTER_MODE = ADDR_REG_ARGUMENT;
endmodule

module Datapath (
  input  [15:0] DATA_IN,
  input  DATAPATH_STARTUP_RESET,
  input  ACC_LOAD,
  input  VALID_IN,
  input  CLK,
  output [15:0] ACC_OUT,
  output ZERO,
  output NEGATIVE,
  output ACC_VALID_OUT
);

  Register #(.width(16)) ACC (.D(DATA_IN), .en(ACC_LOAD), .clk(CLK), .Q(ACC_OUT), .clr(DATAPATH_STARTUP_RESET));
  Register #(.width(1)) ACC_VALID (
    .D(VALID_IN), .en(ACC_LOAD), .clk(CLK), .Q(ACC_VALID_OUT), .clr(DATAPATH_STARTUP_RESET));
  Comparator #(.width(16)) comparator_1 (.a(ACC_OUT), .b({16{1'b0}}), .eq(ZERO), .lt(NEGATIVE));  // open: gt

  // Notes on the sheet:
  //   Clocked 16-bit accumulator; signed comparator derives ZERO and NEGATIVE
endmodule

module AddressPath (
  input  [15:0] ADDRESS_IN,
  input  AR_LOAD,
  input  [15:0] OFFSET,
  input  VALID_IN,
  input  CLK,
  input  ADDRESS_PATH_STARTUP_RESET,
  output [15:0] ADDRESS,
  output [15:0] ADDRESS_PLUS_OFFSET,
  output OFFSET_CARRY,
  output ADDRESS_VALID
);

  Register #(.width(16)) AR (.D(ADDRESS_IN), .en(AR_LOAD), .clk(CLK), .Q(ADDRESS), .clr(ADDRESS_PATH_STARTUP_RESET));
  Register #(.width(1)) AR_VALID (
    .D(VALID_IN), .en(AR_LOAD), .clk(CLK), .Q(ADDRESS_VALID), .clr(ADDRESS_PATH_STARTUP_RESET));
  Adder #(.width(16)) adder_1 (.a(ADDRESS), .b(OFFSET), .out(ADDRESS_PLUS_OFFSET), .cout(OFFSET_CARRY));  // open: cin

  // Notes on the sheet:
  //   Clocked 12-bit address register with combinational offset addition
endmodule

module Memory (
  input  [15:0] ADDRESS,
  input  WRITE_ENABLE,
  input  CLK,
  input  VALID_IN,
  input  [15:0] DATA_IN,
  output MEMORY_VALID,
  output [15:0] MEMORY_DATA
);

  RAM #(.addrWidth(12), .asyncread("true"), .dataWidth(1)) VALID_RAM (
    .addr(ADDRESS[11:0]), .we(WRITE_ENABLE), .oe(1'b1), .clk(CLK), .din(VALID_IN), .dout(MEMORY_VALID));
  RAM #(.addrWidth(12), .asyncread("true"), .dataWidth(16)) DATA_RAM (
    .addr(ADDRESS[11:0]), .we(WRITE_ENABLE), .oe(1'b1), .clk(CLK), .din(DATA_IN), .dout(MEMORY_DATA));

  // Notes on the sheet:
  //   4096-word value/valid memory with shared address, write-enable, and clock
endmodule

module ErrorFlags (
  input  CLEAR_ERROR,
  input  CLK,
  input  SET_OVF,
  input  SET_DIV0,
  input  SET_ADDR,
  input  SET_INV,
  input  SET_ILL,
  input  SET_INPUT,
  output OVF_OUT,
  output DIV0_OUT,
  output ADDR_OUT,
  output INV_OUT,
  output ILL_OUT,
  output INPUT_OUT
);

  wire HOLD_ADDR_out, HOLD_DIV0_out, HOLD_ILL_out, HOLD_INPUT_out, HOLD_INV_out, HOLD_OVF_out, NEXT_ADDR_out,
       NEXT_DIV0_out, NEXT_ILL_out, NEXT_INPUT_out, NEXT_INV_out, NEXT_OVF_out, NOT_CLEAR_ERROR_out;

  not NOT_CLEAR_ERROR (NOT_CLEAR_ERROR_out, CLEAR_ERROR);
  and HOLD_OVF (HOLD_OVF_out, OVF_OUT, NOT_CLEAR_ERROR_out);
  and HOLD_DIV0 (HOLD_DIV0_out, DIV0_OUT, NOT_CLEAR_ERROR_out);
  and HOLD_INV (HOLD_INV_out, INV_OUT, NOT_CLEAR_ERROR_out);
  or NEXT_DIV0 (NEXT_DIV0_out, SET_DIV0, HOLD_DIV0_out);
  and HOLD_ADDR (HOLD_ADDR_out, ADDR_OUT, NOT_CLEAR_ERROR_out);
  and HOLD_ILL (HOLD_ILL_out, ILL_OUT, NOT_CLEAR_ERROR_out);
  and HOLD_INPUT (HOLD_INPUT_out, INPUT_OUT, NOT_CLEAR_ERROR_out);
  or NEXT_OVF (NEXT_OVF_out, SET_OVF, HOLD_OVF_out);
  or NEXT_ADDR (NEXT_ADDR_out, SET_ADDR, HOLD_ADDR_out);
  or NEXT_INV (NEXT_INV_out, SET_INV, HOLD_INV_out);
  or NEXT_ILL (NEXT_ILL_out, SET_ILL, HOLD_ILL_out);
  or NEXT_INPUT (NEXT_INPUT_out, SET_INPUT, HOLD_INPUT_out);
  Register #(.width(1)) OVF (.D(NEXT_OVF_out), .en(1'b1), .clk(CLK), .Q(OVF_OUT), .clr(CLEAR_ERROR));
  Register #(.width(1)) DIV0 (.D(NEXT_DIV0_out), .en(1'b1), .clk(CLK), .Q(DIV0_OUT), .clr(CLEAR_ERROR));
  Register #(.width(1)) ADDR (.D(NEXT_ADDR_out), .en(1'b1), .clk(CLK), .Q(ADDR_OUT), .clr(CLEAR_ERROR));
  Register #(.width(1)) INV (.D(NEXT_INV_out), .en(1'b1), .clk(CLK), .Q(INV_OUT), .clr(CLEAR_ERROR));
  Register #(.width(1)) ILL (.D(NEXT_ILL_out), .en(1'b1), .clk(CLK), .Q(ILL_OUT), .clr(CLEAR_ERROR));
  Register #(.width(1)) INPUT (.D(NEXT_INPUT_out), .en(1'b1), .clk(CLK), .Q(INPUT_OUT), .clr(CLEAR_ERROR));

  // Notes on the sheet:
  //   Set-dominant sticky flags: SET OR (current AND NOT CLEAR_ERROR)
endmodule

module FetchDecode (
  input  CLK,
  input  RESET,
  input  DEC_JUMP_NOT_ZERO,
  input  NOT_ZERO,
  input  [15:0] PROGRAM_LIMIT,
  input  DEC_HALT_ERROR,
  output JUMP_NOT_ZERO,
  output HALT_ERROR,
  output [11:0] PC_OUT,
  output [21:0] OPCODE
);

  wire comparator_1_gt;
  wire [15:0] adder_1_out, multiplexer_1_out;
  wire [15:12] PC_q;

  Register #(.width(16)) PC (.D(multiplexer_1_out), .en(1'b1), .clk(CLK), .Q({PC_q, PC_OUT}), .clr(RESET));
  and JNZ_TAKEN (JUMP_NOT_ZERO, DEC_JUMP_NOT_ZERO, NOT_ZERO);
  Adder #(.width(16)) adder_1 (.a({PC_q, PC_OUT}), .b(16'h1), .out(adder_1_out));  // open: cin, cout
  Comparator #(.width(16)) comparator_1 (.a({PC_q, PC_OUT}), .b(PROGRAM_LIMIT), .gt(comparator_1_gt));  // open: eq, lt
  Multiplexer #(.width(16)) multiplexer_1 (
    .in0(adder_1_out), .in1(OPCODE[15:0]), .out(multiplexer_1_out), .sel(JUMP_NOT_ZERO));
  ROM #(.addrWidth(12), .dataWidth(22)) INSTRUCTION_ROM (.addr(PC_OUT), .data(OPCODE));
  or ERROR_HALT (HALT_ERROR, comparator_1_gt, DEC_HALT_ERROR);

  // Notes on the sheet:
  //   PROGRAM_LIMIT: initial=0xfff
  //   AP 7 machine format v1: stable six-bit opcode allocation and encoder-generated ROM
  //   contents of INSTRUCTION_ROM (hex, n*v repeats v):
  //   ffff 1c0065 3 1c0064 2a0000 4ffff 1c0064 240004 2c0000
endmodule

module FetchDecodeControls (
  input  [5:0] OPCODE,
  output ADD_OPERAND,
  output SUB_OPERAND,
  output MUL_OPERAND,
  output DIV_OPERAND,
  output AND_OPERAND,
  output OR_OPERAND,
  output XOR_OPERAND,
  output LOAD_OPERAND,
  output STORE_OPERAND,
  output CONST_ARGUMENT,
  output ADDR_ARGUMENT,
  output ADDR_REG_ARGUMENT,
  output ADDR_REG_OFFS_ARGUMENT,
  output NOT,
  output JUMP_ADR,
  output JUMP_ZERO,
  output JUMP_NOT_ZERO,
  output JUMP_NEGATIVE,
  output JUMP_ERROR,
  output JUMP_NOT_ERROR,
  output SET_OVF,
  output SET_DIV0,
  output SET_ADDR,
  output SET_INV,
  output SET_ILL,
  output SET_INPUT,
  output CLEAR_ERROR,
  output INPUT,
  output PRINT,
  output PRINT_ADR,
  output HALT,
  output HALT_ERROR,
  output INVALID_OPERAND
);

  wire decoder_1_out4, decoder_1_out5, decoder_1_out6, decoder_1_out7, decoder_2_out8, decoder_2_out9,
       decoder_2_out10, decoder_2_out11, decoder_3_out12, decoder_3_out13, decoder_3_out14, decoder_3_out15,
       decoder_4_out16, decoder_4_out17, decoder_4_out18, decoder_4_out19, decoder_5_out20, decoder_5_out21,
       decoder_5_out22, decoder_5_out23, decoder_6_out24, decoder_6_out25, decoder_6_out26, decoder_6_out27,
       decoder_7_out46, decoder_7_out47, decoder_7_out48, decoder_7_out49, decoder_8_out0, decoder_8_out1,
       decoder_8_out2, decoder_8_out3, decoder_9_out28, decoder_9_out29, decoder_9_out30, decoder_10_out0,
       decoder_10_out4, decoder_10_out8, decoder_10_out12, decoder_10_out16, decoder_10_out20,
       decoder_10_out24, decoder_10_out31, decoder_10_out46, decoder_11_out1, decoder_11_out5,
       decoder_11_out9, decoder_11_out13, decoder_11_out17, decoder_11_out21, decoder_11_out25,
       decoder_11_out28, decoder_11_out32, decoder_11_out43, decoder_11_out47, decoder_12_out2,
       decoder_12_out6, decoder_12_out10, decoder_12_out14, decoder_12_out18, decoder_12_out22,
       decoder_12_out26, decoder_12_out29, decoder_12_out48, decoder_13_out3, decoder_13_out7,
       decoder_13_out11, decoder_13_out15, decoder_13_out19, decoder_13_out23, decoder_13_out27,
       decoder_13_out30, decoder_13_out49, decoder_33_out50, decoder_33_out51, decoder_33_out52,
       decoder_33_out53, decoder_33_out54, decoder_33_out55, decoder_33_out56, decoder_33_out57,
       decoder_33_out58, decoder_33_out59, decoder_33_out60, decoder_33_out61, decoder_33_out62,
       decoder_33_out63;
  wire [5:0] undriven, undriven_2, undriven_3, undriven_4, undriven_5, undriven_6, undriven_7, undriven_8,
       undriven_9, undriven_10, undriven_11, undriven_12, undriven_13, undriven_14, undriven_15, undriven_16,
       undriven_17, undriven_18, undriven_19, undriven_20, undriven_21, undriven_22, undriven_23,
       undriven_24, undriven_25, undriven_26, undriven_27, undriven_28, undriven_29, undriven_30, undriven_31;

  Decoder #(.select(6)) decoder_1 (
    .out4(decoder_1_out4), .out5(decoder_1_out5), .out6(decoder_1_out6), .out7(decoder_1_out7), .sel(OPCODE));  // open: out0, out1, out2, out3, out8, out9, out10, out11, out12, out13, out14, out15, out16, out17, out18, out19, out20, out21, out22, out23, out24, out25, out26, out27, out28, out29, out30, out31, out32, out33, out34, out35, out36, out37, out38, out39, out40, out41, out42, out43, out44, out45, out46, out47, out48, out49, out50, out51, out52, out53, out54, out55, out56, out57, out58, out59, out60, out61, out62, out63, en
  Decoder #(.select(6)) decoder_2 (
    .out8(decoder_2_out8), .out9(decoder_2_out9), .out10(decoder_2_out10), .out11(decoder_2_out11),
    .sel(undriven));  // open: out0, out1, out2, out3, out4, out5, out6, out7, out12, out13, out14, out15, out16, out17, out18, out19, out20, out21, out22, out23, out24, out25, out26, out27, out28, out29, out30, out31, out32, out33, out34, out35, out36, out37, out38, out39, out40, out41, out42, out43, out44, out45, out46, out47, out48, out49, out50, out51, out52, out53, out54, out55, out56, out57, out58, out59, out60, out61, out62, out63, en
  Decoder #(.select(6)) decoder_3 (
    .out12(decoder_3_out12), .out13(decoder_3_out13), .out14(decoder_3_out14), .out15(decoder_3_out15),
    .sel(undriven_2));  // open: out0, out1, out2, out3, out4, out5, out6, out7, out8, out9, out10, out11, out16, out17, out18, out19, out20, out21, out22, out23, out24, out25, out26, out27, out28, out29, out30, out31, out32, out33, out34, out35, out36, out37, out38, out39, out40, out41, out42, out43, out44, out45, out46, out47, out48, out49, out50, out51, out52, out53, out54, out55, out56, out57, out58, out59, out60, out61, out62, out63, en
  Decoder #(.select(6)) decoder_4 (
    .out16(decoder_4_out16), .out17(decoder_4_out17), .out18(decoder_4_out18), .out19(decoder_4_out19),
    .sel(undriven_3));  // open: out0, out1, out2, out3, out4, out5, out6, out7, out8, out9, out10, out11, out12, out13, out14, out15, out20, out21, out22, out23, out24, out25, out26, out27, out28, out29, out30, out31, out32, out33, out34, out35, out36, out37, out38, out39, out40, out41, out42, out43, out44, out45, out46, out47, out48, out49, out50, out51, out52, out53, out54, out55, out56, out57, out58, out59, out60, out61, out62, out63, en
  Decoder #(.select(6)) decoder_5 (
    .out20(decoder_5_out20), .out21(decoder_5_out21), .out22(decoder_5_out22), .out23(decoder_5_out23),
    .sel(undriven_4));  // open: out0, out1, out2, out3, out4, out5, out6, out7, out8, out9, out10, out11, out12, out13, out14, out15, out16, out17, out18, out19, out24, out25, out26, out27, out28, out29, out30, out31, out32, out33, out34, out35, out36, out37, out38, out39, out40, out41, out42, out43, out44, out45, out46, out47, out48, out49, out50, out51, out52, out53, out54, out55, out56, out57, out58, out59, out60, out61, out62, out63, en
  Decoder #(.select(6)) decoder_6 (
    .out24(decoder_6_out24), .out25(decoder_6_out25), .out26(decoder_6_out26), .out27(decoder_6_out27),
    .sel(undriven_5));  // open: out0, out1, out2, out3, out4, out5, out6, out7, out8, out9, out10, out11, out12, out13, out14, out15, out16, out17, out18, out19, out20, out21, out22, out23, out28, out29, out30, out31, out32, out33, out34, out35, out36, out37, out38, out39, out40, out41, out42, out43, out44, out45, out46, out47, out48, out49, out50, out51, out52, out53, out54, out55, out56, out57, out58, out59, out60, out61, out62, out63, en
  Decoder #(.select(6)) decoder_7 (
    .out46(decoder_7_out46), .out47(decoder_7_out47), .out48(decoder_7_out48), .out49(decoder_7_out49),
    .sel(undriven_6));  // open: out0, out1, out2, out3, out4, out5, out6, out7, out8, out9, out10, out11, out12, out13, out14, out15, out16, out17, out18, out19, out20, out21, out22, out23, out24, out25, out26, out27, out28, out29, out30, out31, out32, out33, out34, out35, out36, out37, out38, out39, out40, out41, out42, out43, out44, out45, out50, out51, out52, out53, out54, out55, out56, out57, out58, out59, out60, out61, out62, out63, en
  Decoder #(.select(6)) decoder_8 (
    .out0(decoder_8_out0), .out1(decoder_8_out1), .out2(decoder_8_out2), .out3(decoder_8_out3),
    .sel(undriven_7));  // open: out4, out5, out6, out7, out8, out9, out10, out11, out12, out13, out14, out15, out16, out17, out18, out19, out20, out21, out22, out23, out24, out25, out26, out27, out28, out29, out30, out31, out32, out33, out34, out35, out36, out37, out38, out39, out40, out41, out42, out43, out44, out45, out46, out47, out48, out49, out50, out51, out52, out53, out54, out55, out56, out57, out58, out59, out60, out61, out62, out63, en
  Decoder #(.select(6)) decoder_9 (
    .out28(decoder_9_out28), .out29(decoder_9_out29), .out30(decoder_9_out30), .sel(undriven_8));  // open: out0, out1, out2, out3, out4, out5, out6, out7, out8, out9, out10, out11, out12, out13, out14, out15, out16, out17, out18, out19, out20, out21, out22, out23, out24, out25, out26, out27, out31, out32, out33, out34, out35, out36, out37, out38, out39, out40, out41, out42, out43, out44, out45, out46, out47, out48, out49, out50, out51, out52, out53, out54, out55, out56, out57, out58, out59, out60, out61, out62, out63, en
  Decoder #(.select(6)) decoder_10 (
    .out0(decoder_10_out0), .out4(decoder_10_out4), .out8(decoder_10_out8), .out12(decoder_10_out12),
    .out16(decoder_10_out16), .out20(decoder_10_out20), .out24(decoder_10_out24), .out31(decoder_10_out31),
    .out46(decoder_10_out46), .sel(undriven_9));  // open: out1, out2, out3, out5, out6, out7, out9, out10, out11, out13, out14, out15, out17, out18, out19, out21, out22, out23, out25, out26, out27, out28, out29, out30, out32, out33, out34, out35, out36, out37, out38, out39, out40, out41, out42, out43, out44, out45, out47, out48, out49, out50, out51, out52, out53, out54, out55, out56, out57, out58, out59, out60, out61, out62, out63, en
  Decoder #(.select(6)) decoder_11 (
    .out1(decoder_11_out1), .out5(decoder_11_out5), .out9(decoder_11_out9), .out13(decoder_11_out13),
    .out17(decoder_11_out17), .out21(decoder_11_out21), .out25(decoder_11_out25), .out28(decoder_11_out28),
    .out32(decoder_11_out32), .out43(decoder_11_out43), .out47(decoder_11_out47), .sel(undriven_10));  // open: out0, out2, out3, out4, out6, out7, out8, out10, out11, out12, out14, out15, out16, out18, out19, out20, out22, out23, out24, out26, out27, out29, out30, out31, out33, out34, out35, out36, out37, out38, out39, out40, out41, out42, out44, out45, out46, out48, out49, out50, out51, out52, out53, out54, out55, out56, out57, out58, out59, out60, out61, out62, out63, en
  Decoder #(.select(6)) decoder_12 (
    .out2(decoder_12_out2), .out6(decoder_12_out6), .out10(decoder_12_out10), .out14(decoder_12_out14),
    .out18(decoder_12_out18), .out22(decoder_12_out22), .out26(decoder_12_out26), .out29(decoder_12_out29),
    .out48(decoder_12_out48), .sel(undriven_11));  // open: out0, out1, out3, out4, out5, out7, out8, out9, out11, out12, out13, out15, out16, out17, out19, out20, out21, out23, out24, out25, out27, out28, out30, out31, out32, out33, out34, out35, out36, out37, out38, out39, out40, out41, out42, out43, out44, out45, out46, out47, out49, out50, out51, out52, out53, out54, out55, out56, out57, out58, out59, out60, out61, out62, out63, en
  Decoder #(.select(6)) decoder_13 (
    .out3(decoder_13_out3), .out7(decoder_13_out7), .out11(decoder_13_out11), .out15(decoder_13_out15),
    .out19(decoder_13_out19), .out23(decoder_13_out23), .out27(decoder_13_out27), .out30(decoder_13_out30),
    .out49(decoder_13_out49), .sel(undriven_12));  // open: out0, out1, out2, out4, out5, out6, out8, out9, out10, out12, out13, out14, out16, out17, out18, out20, out21, out22, out24, out25, out26, out28, out29, out31, out32, out33, out34, out35, out36, out37, out38, out39, out40, out41, out42, out43, out44, out45, out46, out47, out48, out50, out51, out52, out53, out54, out55, out56, out57, out58, out59, out60, out61, out62, out63, en
  Decoder #(.select(6)) decoder_14 (
    .out33(NOT), .sel(undriven_13));  // open: out0, out1, out2, out3, out4, out5, out6, out7, out8, out9, out10, out11, out12, out13, out14, out15, out16, out17, out18, out19, out20, out21, out22, out23, out24, out25, out26, out27, out28, out29, out30, out31, out32, out34, out35, out36, out37, out38, out39, out40, out41, out42, out43, out44, out45, out46, out47, out48, out49, out50, out51, out52, out53, out54, out55, out56, out57, out58, out59, out60, out61, out62, out63, en
  Decoder #(.select(6)) decoder_15 (
    .out34(JUMP_ADR), .sel(undriven_14));  // open: out0, out1, out2, out3, out4, out5, out6, out7, out8, out9, out10, out11, out12, out13, out14, out15, out16, out17, out18, out19, out20, out21, out22, out23, out24, out25, out26, out27, out28, out29, out30, out31, out32, out33, out35, out36, out37, out38, out39, out40, out41, out42, out43, out44, out45, out46, out47, out48, out49, out50, out51, out52, out53, out54, out55, out56, out57, out58, out59, out60, out61, out62, out63, en
  Decoder #(.select(6)) decoder_16 (
    .out35(JUMP_ZERO), .sel(undriven_15));  // open: out0, out1, out2, out3, out4, out5, out6, out7, out8, out9, out10, out11, out12, out13, out14, out15, out16, out17, out18, out19, out20, out21, out22, out23, out24, out25, out26, out27, out28, out29, out30, out31, out32, out33, out34, out36, out37, out38, out39, out40, out41, out42, out43, out44, out45, out46, out47, out48, out49, out50, out51, out52, out53, out54, out55, out56, out57, out58, out59, out60, out61, out62, out63, en
  Decoder #(.select(6)) decoder_17 (
    .out36(JUMP_NOT_ZERO), .sel(undriven_16));  // open: out0, out1, out2, out3, out4, out5, out6, out7, out8, out9, out10, out11, out12, out13, out14, out15, out16, out17, out18, out19, out20, out21, out22, out23, out24, out25, out26, out27, out28, out29, out30, out31, out32, out33, out34, out35, out37, out38, out39, out40, out41, out42, out43, out44, out45, out46, out47, out48, out49, out50, out51, out52, out53, out54, out55, out56, out57, out58, out59, out60, out61, out62, out63, en
  Decoder #(.select(6)) decoder_18 (
    .out37(JUMP_NEGATIVE), .sel(undriven_17));  // open: out0, out1, out2, out3, out4, out5, out6, out7, out8, out9, out10, out11, out12, out13, out14, out15, out16, out17, out18, out19, out20, out21, out22, out23, out24, out25, out26, out27, out28, out29, out30, out31, out32, out33, out34, out35, out36, out38, out39, out40, out41, out42, out43, out44, out45, out46, out47, out48, out49, out50, out51, out52, out53, out54, out55, out56, out57, out58, out59, out60, out61, out62, out63, en
  Decoder #(.select(6)) decoder_19 (
    .out38(JUMP_ERROR), .sel(undriven_18));  // open: out0, out1, out2, out3, out4, out5, out6, out7, out8, out9, out10, out11, out12, out13, out14, out15, out16, out17, out18, out19, out20, out21, out22, out23, out24, out25, out26, out27, out28, out29, out30, out31, out32, out33, out34, out35, out36, out37, out39, out40, out41, out42, out43, out44, out45, out46, out47, out48, out49, out50, out51, out52, out53, out54, out55, out56, out57, out58, out59, out60, out61, out62, out63, en
  Decoder #(.select(6)) decoder_20 (
    .out39(JUMP_NOT_ERROR), .sel(undriven_19));  // open: out0, out1, out2, out3, out4, out5, out6, out7, out8, out9, out10, out11, out12, out13, out14, out15, out16, out17, out18, out19, out20, out21, out22, out23, out24, out25, out26, out27, out28, out29, out30, out31, out32, out33, out34, out35, out36, out37, out38, out40, out41, out42, out43, out44, out45, out46, out47, out48, out49, out50, out51, out52, out53, out54, out55, out56, out57, out58, out59, out60, out61, out62, out63, en
  Decoder #(.select(6)) decoder_21 (.sel(undriven_20));  // open: out0, out1, out2, out3, out4, out5, out6, out7, out8, out9, out10, out11, out12, out13, out14, out15, out16, out17, out18, out19, out20, out21, out22, out23, out24, out25, out26, out27, out28, out29, out30, out31, out32, out33, out34, out35, out36, out37, out38, out39, out40, out41, out42, out43, out44, out45, out46, out47, out48, out49, out50, out51, out52, out53, out54, out55, out56, out57, out58, out59, out60, out61, out62, out63, en
  Decoder #(.select(6)) decoder_22 (.sel(undriven_21));  // open: out0, out1, out2, out3, out4, out5, out6, out7, out8, out9, out10, out11, out12, out13, out14, out15, out16, out17, out18, out19, out20, out21, out22, out23, out24, out25, out26, out27, out28, out29, out30, out31, out32, out33, out34, out35, out36, out37, out38, out39, out40, out41, out42, out43, out44, out45, out46, out47, out48, out49, out50, out51, out52, out53, out54, out55, out56, out57, out58, out59, out60, out61, out62, out63, en
  Decoder #(.select(6)) decoder_23 (.sel(undriven_22));  // open: out0, out1, out2, out3, out4, out5, out6, out7, out8, out9, out10, out11, out12, out13, out14, out15, out16, out17, out18, out19, out20, out21, out22, out23, out24, out25, out26, out27, out28, out29, out30, out31, out32, out33, out34, out35, out36, out37, out38, out39, out40, out41, out42, out43, out44, out45, out46, out47, out48, out49, out50, out51, out52, out53, out54, out55, out56, out57, out58, out59, out60, out61, out62, out63, en
  Decoder #(.select(6)) decoder_24 (.sel(undriven_23));  // open: out0, out1, out2, out3, out4, out5, out6, out7, out8, out9, out10, out11, out12, out13, out14, out15, out16, out17, out18, out19, out20, out21, out22, out23, out24, out25, out26, out27, out28, out29, out30, out31, out32, out33, out34, out35, out36, out37, out38, out39, out40, out41, out42, out43, out44, out45, out46, out47, out48, out49, out50, out51, out52, out53, out54, out55, out56, out57, out58, out59, out60, out61, out62, out63, en
  Decoder #(.select(6)) decoder_25 (.sel(undriven_24));  // open: out0, out1, out2, out3, out4, out5, out6, out7, out8, out9, out10, out11, out12, out13, out14, out15, out16, out17, out18, out19, out20, out21, out22, out23, out24, out25, out26, out27, out28, out29, out30, out31, out32, out33, out34, out35, out36, out37, out38, out39, out40, out41, out42, out43, out44, out45, out46, out47, out48, out49, out50, out51, out52, out53, out54, out55, out56, out57, out58, out59, out60, out61, out62, out63, en
  Decoder #(.select(6)) decoder_26 (.sel(undriven_25));  // open: out0, out1, out2, out3, out4, out5, out6, out7, out8, out9, out10, out11, out12, out13, out14, out15, out16, out17, out18, out19, out20, out21, out22, out23, out24, out25, out26, out27, out28, out29, out30, out31, out32, out33, out34, out35, out36, out37, out38, out39, out40, out41, out42, out43, out44, out45, out46, out47, out48, out49, out50, out51, out52, out53, out54, out55, out56, out57, out58, out59, out60, out61, out62, out63, en
  Decoder #(.select(6)) decoder_27 (
    .out40(CLEAR_ERROR), .sel(undriven_26));  // open: out0, out1, out2, out3, out4, out5, out6, out7, out8, out9, out10, out11, out12, out13, out14, out15, out16, out17, out18, out19, out20, out21, out22, out23, out24, out25, out26, out27, out28, out29, out30, out31, out32, out33, out34, out35, out36, out37, out38, out39, out41, out42, out43, out44, out45, out46, out47, out48, out49, out50, out51, out52, out53, out54, out55, out56, out57, out58, out59, out60, out61, out62, out63, en
  Decoder #(.select(6)) decoder_28 (
    .out41(INPUT), .sel(undriven_27));  // open: out0, out1, out2, out3, out4, out5, out6, out7, out8, out9, out10, out11, out12, out13, out14, out15, out16, out17, out18, out19, out20, out21, out22, out23, out24, out25, out26, out27, out28, out29, out30, out31, out32, out33, out34, out35, out36, out37, out38, out39, out40, out42, out43, out44, out45, out46, out47, out48, out49, out50, out51, out52, out53, out54, out55, out56, out57, out58, out59, out60, out61, out62, out63, en
  Decoder #(.select(6)) decoder_29 (
    .out42(PRINT), .sel(undriven_28));  // open: out0, out1, out2, out3, out4, out5, out6, out7, out8, out9, out10, out11, out12, out13, out14, out15, out16, out17, out18, out19, out20, out21, out22, out23, out24, out25, out26, out27, out28, out29, out30, out31, out32, out33, out34, out35, out36, out37, out38, out39, out40, out41, out43, out44, out45, out46, out47, out48, out49, out50, out51, out52, out53, out54, out55, out56, out57, out58, out59, out60, out61, out62, out63, en
  Decoder #(.select(6)) decoder_30 (
    .out43(PRINT_ADR), .sel(undriven_29));  // open: out0, out1, out2, out3, out4, out5, out6, out7, out8, out9, out10, out11, out12, out13, out14, out15, out16, out17, out18, out19, out20, out21, out22, out23, out24, out25, out26, out27, out28, out29, out30, out31, out32, out33, out34, out35, out36, out37, out38, out39, out40, out41, out42, out44, out45, out46, out47, out48, out49, out50, out51, out52, out53, out54, out55, out56, out57, out58, out59, out60, out61, out62, out63, en
  Decoder #(.select(6)) decoder_31 (
    .out44(HALT), .sel(undriven_30));  // open: out0, out1, out2, out3, out4, out5, out6, out7, out8, out9, out10, out11, out12, out13, out14, out15, out16, out17, out18, out19, out20, out21, out22, out23, out24, out25, out26, out27, out28, out29, out30, out31, out32, out33, out34, out35, out36, out37, out38, out39, out40, out41, out42, out43, out45, out46, out47, out48, out49, out50, out51, out52, out53, out54, out55, out56, out57, out58, out59, out60, out61, out62, out63, en
  Decoder #(.select(6)) decoder_32 (
    .out45(HALT_ERROR), .sel(undriven_31));  // open: out0, out1, out2, out3, out4, out5, out6, out7, out8, out9, out10, out11, out12, out13, out14, out15, out16, out17, out18, out19, out20, out21, out22, out23, out24, out25, out26, out27, out28, out29, out30, out31, out32, out33, out34, out35, out36, out37, out38, out39, out40, out41, out42, out43, out44, out46, out47, out48, out49, out50, out51, out52, out53, out54, out55, out56, out57, out58, out59, out60, out61, out62, out63, en
  Decoder #(.select(6)) decoder_33 (
    .out50(decoder_33_out50), .out51(decoder_33_out51), .out52(decoder_33_out52), .out53(decoder_33_out53),
    .out54(decoder_33_out54), .out55(decoder_33_out55), .out56(decoder_33_out56), .out57(decoder_33_out57),
    .out58(decoder_33_out58), .out59(decoder_33_out59), .out60(decoder_33_out60), .out61(decoder_33_out61),
    .out62(decoder_33_out62), .out63(decoder_33_out63), .sel(OPCODE));  // open: out0, out1, out2, out3, out4, out5, out6, out7, out8, out9, out10, out11, out12, out13, out14, out15, out16, out17, out18, out19, out20, out21, out22, out23, out24, out25, out26, out27, out28, out29, out30, out31, out32, out33, out34, out35, out36, out37, out38, out39, out40, out41, out42, out43, out44, out45, out46, out47, out48, out49, en
  or ADD_OPERAND_SELECT (ADD_OPERAND, decoder_1_out4, decoder_1_out5, decoder_1_out6, decoder_1_out7);
  or SUB_OPERAND_SELECT (SUB_OPERAND, decoder_2_out8, decoder_2_out9, decoder_2_out10, decoder_2_out11);
  or MUL_OPERAND_SELECT (MUL_OPERAND, decoder_3_out12, decoder_3_out13, decoder_3_out14, decoder_3_out15);
  or DIV_OPERAND_SELECT (DIV_OPERAND, decoder_4_out16, decoder_4_out17, decoder_4_out18, decoder_4_out19);
  or AND_OPERAND_SELECT (AND_OPERAND, decoder_5_out20, decoder_5_out21, decoder_5_out22, decoder_5_out23);
  or OR_OPERAND_SELECT (OR_OPERAND, decoder_6_out24, decoder_6_out25, decoder_6_out26, decoder_6_out27);
  or XOR_OPERAND_SELECT (XOR_OPERAND, decoder_7_out46, decoder_7_out47, decoder_7_out48, decoder_7_out49);
  or LOAD_OPERAND_SELECT (LOAD_OPERAND, decoder_8_out0, decoder_8_out1, decoder_8_out2, decoder_8_out3);
  or STORE_OPERAND_SELECT (STORE_OPERAND, decoder_9_out28, decoder_9_out29, decoder_9_out30);
  or CONST_ARGUMENT_SELECT (CONST_ARGUMENT, decoder_10_out0, decoder_10_out4, decoder_10_out8, decoder_10_out12, decoder_10_out16, decoder_10_out20, decoder_10_out24, decoder_10_out31, decoder_10_out46);
  or ADDR_ARGUMENT_SELECT (ADDR_ARGUMENT, decoder_11_out1, decoder_11_out5, decoder_11_out9, decoder_11_out13, decoder_11_out17, decoder_11_out21, decoder_11_out25, decoder_11_out28, decoder_11_out32, decoder_11_out43, decoder_11_out47);
  or ADDR_REG_ARGUMENT_SELECT (ADDR_REG_ARGUMENT, decoder_12_out2, decoder_12_out6, decoder_12_out10, decoder_12_out14, decoder_12_out18, decoder_12_out22, decoder_12_out26, decoder_12_out29, decoder_12_out48);
  or ADDR_REG_OFFS_ARGUMENT_SELECT (ADDR_REG_OFFS_ARGUMENT, decoder_13_out3, decoder_13_out7, decoder_13_out11, decoder_13_out15, decoder_13_out19, decoder_13_out23, decoder_13_out27, decoder_13_out30, decoder_13_out49);
  or INVALID_OPERAND_SELECT (INVALID_OPERAND, decoder_33_out50, decoder_33_out51, decoder_33_out52, decoder_33_out53, decoder_33_out54, decoder_33_out55, decoder_33_out56, decoder_33_out57, decoder_33_out58, decoder_33_out59, decoder_33_out60, decoder_33_out61, decoder_33_out62, decoder_33_out63);

  assign SET_ADDR = 1'b0;
  assign SET_DIV0 = 1'b0;
  assign SET_ILL = 1'b0;
  assign SET_INPUT = 1'b0;
  assign SET_INV = 1'b0;
  assign SET_OVF = 1'b0;

  // Notes on the sheet:
  //   ADD_OPERAND: decoder output
  //   SUB_OPERAND: decoder output
  //   MUL_OPERAND: decoder output
  //   DIV_OPERAND: decoder output
  //   AND_OPERAND: decoder output
  //   OR_OPERAND: decoder output
  //   XOR_OPERAND: decoder output
  //   LOAD_OPERAND: decoder output
  //   STORE_OPERAND: decoder output
  //   CONST_ARGUMENT: decoder output
  //   ADDR_ARGUMENT: decoder output
  //   ADDR_REG_ARGUMENT: decoder output
  //   ADDR_REG_OFFS_ARGUMENT: decoder output
  //   NOT: decoder output
  //   JUMP_ADR: decoder output
  //   JUMP_ZERO: decoder output
  //   JUMP_NOT_ZERO: decoder output
  //   JUMP_NEGATIVE: decoder output
  //   JUMP_ERROR: decoder output
  //   JUMP_NOT_ERROR: decoder output
  //   SET_OVF: decoder output
  //   SET_DIV0: decoder output
  //   SET_ADDR: decoder output
  //   SET_INV: decoder output
  //   SET_ILL: decoder output
  //   SET_INPUT: decoder output
  //   CLEAR_ERROR: decoder output
  //   INPUT: decoder output
  //   PRINT: decoder output
  //   PRINT_ADR: decoder output
  //   HALT: decoder output
  //   HALT_ERROR: decoder output
  //   INVALID_OPERAND: decoder output
endmodule

module IntegrationClock (
  input  CLK,
  output FETCH_CLK,
  output DATAPATH_CLK,
  output ADDRESS_CLK,
  output MEMORY_CLK,
  output ERROR_FLAGS_CLK
);


  assign ADDRESS_CLK = CLK;
  assign DATAPATH_CLK = CLK;
  assign ERROR_FLAGS_CLK = CLK;
  assign FETCH_CLK = CLK;
  assign MEMORY_CLK = CLK;
endmodule

module IntegrationReset (
  input  RESET,
  output FETCH_RESET
);


  assign FETCH_RESET = RESET;
endmodule

module AndArithmeticCircuit (
  input  AND_ACTIVATED,
  input  [15:0] LEFT,
  input  [15:0] RIGHT,
  input  INPUT_VALID,
  output [15:0] RESULT,
  output RESULT_VALID
);

  wire [15:0] BITWISE_AND_out;

  assign BITWISE_AND_out = LEFT & RIGHT;  // AND_Gate BITWISE_AND, 16 bits wide
  Multiplexer #(.width(16)) multiplexer_1 (.in0({16{1'b0}}), .in1(BITWISE_AND_out), .out(RESULT), .sel(AND_ACTIVATED));
  and ACTIVE_AND_VALID (RESULT_VALID, AND_ACTIVATED, INPUT_VALID);

  // Notes on the sheet:
  //   bitwise AND: inactive outputs are neutral
endmodule

module Operations (
  input  [15:0] ACC_VALUE,
  input  [15:0] MEMORY_VALUE,
  input  [15:0] IMMEDIATE_VALUE,
  input  MEMORY_VALID,
  input  ACC_VALID,
  input  CONST_OPERAND,
  input  ADD_OPERAND,
  input  SUB_OPERAND,
  input  MUL_OPERAND,
  input  DIV_OPERAND,
  input  AND_OPERAND,
  input  OR_OPERAND,
  input  XOR_OPERAND,
  input  NOT_OPERAND,
  output [15:0] RESULT_VALUE,
  output OVERFLOW,
  output RESULT_IS_VALID,
  output INVALID_OPERAND,
  output DIVIDE_BY_ZERO
);

  wire ACC_ADD_VALID_out, ADD_OPERATION_overflow, ADD_OPERATION_result_valid, AND_OPERATION_result_valid,
       DIV_OPERATION_result_valid, MUL_OPERATION_overflow, MUL_OPERATION_result_valid, multiplexer_1_out,
       not_1_out, NOT_OPERATION_result_valid, OPERATION_IS_ACTIVE_out, OPERATION_RESULT_VALID_out,
       OR_OPERATION_result_valid, SUB_OPERATION_overflow, SUB_OPERATION_result_valid,
       XOR_OPERATION_result_valid;
  wire [15:0] ADD_OPERATION_result, AND_OPERATION_result, DIV_OPERATION_result, MUL_OPERATION_result,
       multiplexer_2_out, NOT_OPERATION_result, OR_OPERATION_result, RESULT_out, SUB_OPERATION_result,
       XOR_OPERATION_result;

  Multiplexer multiplexer_1 (.in0(MEMORY_VALID), .in1(1'b1), .out(multiplexer_1_out), .sel(CONST_OPERAND));
  Multiplexer #(.width(16)) multiplexer_2 (
    .in0(MEMORY_VALUE), .in1(IMMEDIATE_VALUE), .out(multiplexer_2_out), .sel(CONST_OPERAND));
  and ACC_ADD_VALID (ACC_ADD_VALID_out, multiplexer_1_out, ACC_VALID);
  AddArithmeticCircuit ADD_OPERATION (
    .ADD_ACTIVATED(ADD_OPERAND), .LEFT(ACC_VALUE), .RIGHT(multiplexer_2_out),
    .INPUT_VALID(ACC_ADD_VALID_out), .RESULT(ADD_OPERATION_result), .OVERFLOW(ADD_OPERATION_overflow),
    .RESULT_VALID(ADD_OPERATION_result_valid));
  SubArithmeticCircuit SUB_OPERATION (
    .SUB_ACTIVATED(SUB_OPERAND), .LEFT(ACC_VALUE), .RIGHT(multiplexer_2_out),
    .INPUT_VALID(ACC_ADD_VALID_out), .RESULT(SUB_OPERATION_result), .OVERFLOW(SUB_OPERATION_overflow),
    .RESULT_VALID(SUB_OPERATION_result_valid));
  MulArithmeticCircuit MUL_OPERATION (
    .MUL_ACTIVATED(MUL_OPERAND), .LEFT(ACC_VALUE), .RIGHT(multiplexer_2_out),
    .INPUT_VALID(ACC_ADD_VALID_out), .RESULT(MUL_OPERATION_result), .OVERFLOW(MUL_OPERATION_overflow),
    .RESULT_VALID(MUL_OPERATION_result_valid));
  DivArithmeticCircuit DIV_OPERATION (
    .DIV_ACTIVATED(DIV_OPERAND), .LEFT(ACC_VALUE), .RIGHT(multiplexer_2_out),
    .INPUT_VALID(ACC_ADD_VALID_out), .RESULT(DIV_OPERATION_result),
    .RESULT_VALID(DIV_OPERATION_result_valid), .DIVIDE_BY_ZERO(DIVIDE_BY_ZERO));
  AndArithmeticCircuit AND_OPERATION (
    .AND_ACTIVATED(AND_OPERAND), .LEFT(ACC_VALUE), .RIGHT(multiplexer_2_out),
    .INPUT_VALID(ACC_ADD_VALID_out), .RESULT(AND_OPERATION_result), .RESULT_VALID(AND_OPERATION_result_valid));
  OrArithmeticCircuit OR_OPERATION (
    .OR_ACTIVATED(OR_OPERAND), .LEFT(ACC_VALUE), .RIGHT(multiplexer_2_out), .INPUT_VALID(ACC_ADD_VALID_out),
    .RESULT(OR_OPERATION_result), .RESULT_VALID(OR_OPERATION_result_valid));
  XorArithmeticCircuit XOR_OPERATION (
    .XOR_ACTIVATED(XOR_OPERAND), .LEFT(ACC_VALUE), .RIGHT(multiplexer_2_out),
    .INPUT_VALID(ACC_ADD_VALID_out), .RESULT(XOR_OPERATION_result), .RESULT_VALID(XOR_OPERATION_result_valid));
  NotCircuit NOT_OPERATION (
    .NOT_IS_ACTIVE(NOT_OPERAND), .ACC_VALUE(ACC_VALUE), .ACC_VALID(ACC_ADD_VALID_out),
    .RESULT(NOT_OPERATION_result), .RESULT_VALID(NOT_OPERATION_result_valid));
  assign RESULT_out = ADD_OPERATION_result | SUB_OPERATION_result | MUL_OPERATION_result | DIV_OPERATION_result | AND_OPERATION_result | OR_OPERATION_result | XOR_OPERATION_result | NOT_OPERATION_result;  // OR_Gate RESULT, 16 bits wide
  or OVERFLOW_SET (OVERFLOW, ADD_OPERATION_overflow, SUB_OPERATION_overflow, MUL_OPERATION_overflow);
  or OPERATION_RESULT_VALID (OPERATION_RESULT_VALID_out, ADD_OPERATION_result_valid, SUB_OPERATION_result_valid, MUL_OPERATION_result_valid, DIV_OPERATION_result_valid, AND_OPERATION_result_valid, OR_OPERATION_result_valid, XOR_OPERATION_result_valid, NOT_OPERATION_result_valid);
  or OPERATION_IS_ACTIVE (OPERATION_IS_ACTIVE_out, ADD_OPERAND, SUB_OPERAND, MUL_OPERAND, DIV_OPERAND, AND_OPERAND, OR_OPERAND, XOR_OPERAND, NOT_OPERAND);
  not not_1 (not_1_out, OPERATION_RESULT_VALID_out);
  Multiplexer #(.width(16)) multiplexer_3 (
    .in0(multiplexer_2_out), .in1(RESULT_out), .out(RESULT_VALUE), .sel(OPERATION_IS_ACTIVE_out));
  Multiplexer multiplexer_4 (
    .in0(ACC_ADD_VALID_out), .in1(OPERATION_RESULT_VALID_out), .out(RESULT_IS_VALID),
    .sel(OPERATION_IS_ACTIVE_out));
  and ACTIVE_INVALID_OPERATION (INVALID_OPERAND, not_1_out, OPERATION_IS_ACTIVE_out);
endmodule

module NotCircuit (
  input  NOT_IS_ACTIVE,
  input  [15:0] ACC_VALUE,
  input  ACC_VALID,
  output [15:0] RESULT,
  output RESULT_VALID
);

  wire [15:0] NOT_VALUE_out;

  assign NOT_VALUE_out = ~ACC_VALUE;  // NOT_Gate NOT_VALUE, 16 bits wide
  Multiplexer #(.width(16)) multiplexer_1 (.in0({16{1'b0}}), .in1(NOT_VALUE_out), .out(RESULT), .sel(NOT_IS_ACTIVE));
  and ACTIVE_NOT_VALID (RESULT_VALID, ACC_VALID, NOT_IS_ACTIVE);
endmodule

module MulArithmeticCircuit (
  input  MUL_ACTIVATED,
  input  [15:0] LEFT,
  input  [15:0] RIGHT,
  input  INPUT_VALID,
  output [15:0] RESULT,
  output OVERFLOW,
  output RESULT_VALID
);

  wire NO_OVERFLOW_out, OPERAND_SIGN_DIFFERENT_out, RESULT_SIGN_CHANGED_out;
  wire [14:0] multiplexer_2_out;
  wire [15:0] multiplexer_1_out;
  wire [15:15] multiplexer_2_out_2;

  Multiplexer #(.width(16)) multiplexer_1 (.in0({16{1'b0}}), .in1(LEFT), .out(multiplexer_1_out), .sel(MUL_ACTIVATED));
  Multiplexer #(.width(16)) multiplexer_2 (
    .in0({16{1'b0}}), .in1(RIGHT), .out({multiplexer_2_out_2[15], multiplexer_2_out}), .sel(MUL_ACTIVATED));
  Multiplier #(.width(16)) multiplier_1 (
    .a(multiplexer_1_out), .b({multiplexer_2_out_2[15], multiplexer_2_out}), .out(RESULT));  // open: cin, cout
  xor OPERAND_SIGN_DIFFERENT (OPERAND_SIGN_DIFFERENT_out, multiplexer_1_out[15], multiplexer_2_out_2[15]);
  xor RESULT_SIGN_CHANGED (RESULT_SIGN_CHANGED_out, RESULT[15], multiplexer_1_out[15]);
  not NO_OVERFLOW (NO_OVERFLOW_out, OPERAND_SIGN_DIFFERENT_out);
  and SIGN_OVERFLOW (OVERFLOW, RESULT_SIGN_CHANGED_out, OPERAND_SIGN_DIFFERENT_out);
  and RANGE_VALID (RESULT_VALID, NO_OVERFLOW_out, INPUT_VALID);

  // Notes on the sheet:
  //   signed MUL: overflow = (left_sign XOR right_sign) AND (left_sign XOR result_sign)
endmodule

module DivArithmeticCircuit (
  input  DIV_ACTIVATED,
  input  [15:0] LEFT,
  input  [15:0] RIGHT,
  input  INPUT_VALID,
  output [15:0] RESULT,
  output RESULT_VALID,
  output DIVIDE_BY_ZERO
);

  wire comparator_1_gt, NONZERO_DIVISOR_out;
  wire [15:0] multiplexer_1_out, multiplexer_2_out;

  Multiplexer #(.width(16)) multiplexer_1 (.in0({16{1'b0}}), .in1(LEFT), .out(multiplexer_1_out), .sel(DIV_ACTIVATED));
  Multiplexer #(.width(16)) multiplexer_2 (.in0(16'h1), .in1(RIGHT), .out(multiplexer_2_out), .sel(DIV_ACTIVATED));
  Divider #(.mode("twosComplement"), .width(16)) divider_1 (
    .a(multiplexer_1_out), .b(multiplexer_2_out), .out(RESULT));  // open: upper, rem
  Comparator #(.width(16)) comparator_1 (.a(multiplexer_2_out), .b(16'h1), .gt(comparator_1_gt));  // open: eq, lt
  not NONZERO_DIVISOR (NONZERO_DIVISOR_out, comparator_1_gt);
  and RANGE_VALID (RESULT_VALID, comparator_1_gt, DIV_ACTIVATED, INPUT_VALID);
  and DIVIDE_BY_ZERO_ACTIVE (DIVIDE_BY_ZERO, NONZERO_DIVISOR_out, DIV_ACTIVATED);
endmodule

module AddArithmeticCircuit (
  input  ADD_ACTIVATED,
  input  [15:0] LEFT,
  input  [15:0] RIGHT,
  input  INPUT_VALID,
  output [15:0] RESULT,
  output OVERFLOW,
  output RESULT_VALID
);

  wire NO_OVERFLOW_out, OPERAND_SIGN_DIFFERENT_out, OPERAND_SIGN_SAME_out, RESULT_SIGN_CHANGED_out;
  wire [14:0] multiplexer_2_out;
  wire [15:0] multiplexer_1_out;
  wire [15:15] multiplexer_2_out_2;

  Multiplexer #(.width(16)) multiplexer_1 (.in0({16{1'b0}}), .in1(LEFT), .out(multiplexer_1_out), .sel(ADD_ACTIVATED));
  Multiplexer #(.width(16)) multiplexer_2 (
    .in0({16{1'b0}}), .in1(RIGHT), .out({multiplexer_2_out_2[15], multiplexer_2_out}), .sel(ADD_ACTIVATED));
  Adder #(.width(16)) adder_1 (
    .a(multiplexer_1_out), .b({multiplexer_2_out_2[15], multiplexer_2_out}), .out(RESULT));  // open: cin, cout
  xor OPERAND_SIGN_DIFFERENT (OPERAND_SIGN_DIFFERENT_out, multiplexer_1_out[15], multiplexer_2_out_2[15]);
  not OPERAND_SIGN_SAME (OPERAND_SIGN_SAME_out, OPERAND_SIGN_DIFFERENT_out);
  xor RESULT_SIGN_CHANGED (RESULT_SIGN_CHANGED_out, RESULT[15], multiplexer_1_out[15]);
  not NO_OVERFLOW (NO_OVERFLOW_out, OPERAND_SIGN_SAME_out);
  and SIGN_OVERFLOW (OVERFLOW, RESULT_SIGN_CHANGED_out, OPERAND_SIGN_SAME_out);
  and RANGE_VALID (RESULT_VALID, NO_OVERFLOW_out, ADD_ACTIVATED, INPUT_VALID);

  // Notes on the sheet:
  //   signed ADD: overflow = NOT(left_sign XOR right_sign) AND (left_sign XOR result_sign)
endmodule

module SubArithmeticCircuit (
  input  SUB_ACTIVATED,
  input  [15:0] LEFT,
  input  [15:0] RIGHT,
  input  INPUT_VALID,
  output [15:0] RESULT,
  output OVERFLOW,
  output RESULT_VALID
);

  wire NO_OVERFLOW_out, OPERAND_SIGN_DIFFERENT_out, RESULT_SIGN_CHANGED_out;
  wire [14:0] multiplexer_2_out;
  wire [15:0] multiplexer_1_out;
  wire [15:15] multiplexer_2_out_2;

  Multiplexer #(.width(16)) multiplexer_1 (.in0({16{1'b0}}), .in1(LEFT), .out(multiplexer_1_out), .sel(SUB_ACTIVATED));
  Multiplexer #(.width(16)) multiplexer_2 (
    .in0({16{1'b0}}), .in1(RIGHT), .out({multiplexer_2_out_2[15], multiplexer_2_out}), .sel(SUB_ACTIVATED));
  Subtractor #(.width(16)) subtractor_1 (
    .a(multiplexer_1_out), .b({multiplexer_2_out_2[15], multiplexer_2_out}), .out(RESULT));  // open: bin, bout
  xor OPERAND_SIGN_DIFFERENT (OPERAND_SIGN_DIFFERENT_out, multiplexer_1_out[15], multiplexer_2_out_2[15]);
  xor RESULT_SIGN_CHANGED (RESULT_SIGN_CHANGED_out, RESULT[15], multiplexer_1_out[15]);
  not NO_OVERFLOW (NO_OVERFLOW_out, OPERAND_SIGN_DIFFERENT_out);
  and SIGN_OVERFLOW (OVERFLOW, RESULT_SIGN_CHANGED_out, OPERAND_SIGN_DIFFERENT_out);
  and RANGE_VALID (RESULT_VALID, NO_OVERFLOW_out, SUB_ACTIVATED, INPUT_VALID);

  // Notes on the sheet:
  //   signed SUB: overflow = (left_sign XOR right_sign) AND (left_sign XOR result_sign)
endmodule

module AddressRangeFBox (
  input  OFFSET_CARRY,
  input  EFFECTIVE_REGISTER_MODE,
  input  EFFECTIVE_OFFSET_MODE,
  input  ADDRESS_OUT_OF_RANGE,
  input  ADDRESS_OPERAND,
  output ACTIVE_ADDRESS_OUT_OF_RANGE
);

  wire ACTIVE_ADDRESS_RANGE_GATE_out, ACTIVE_OFFSET_ADDRESS_ERROR_out, MEMORY_ADDRESS_ACTIVE_out;

  or MEMORY_ADDRESS_ACTIVE (MEMORY_ADDRESS_ACTIVE_out, ADDRESS_OPERAND, EFFECTIVE_REGISTER_MODE, EFFECTIVE_OFFSET_MODE);
  and ACTIVE_ADDRESS_RANGE_GATE (ACTIVE_ADDRESS_RANGE_GATE_out, MEMORY_ADDRESS_ACTIVE_out, ADDRESS_OUT_OF_RANGE);
  and ACTIVE_OFFSET_ADDRESS_ERROR (ACTIVE_OFFSET_ADDRESS_ERROR_out, OFFSET_CARRY, EFFECTIVE_OFFSET_MODE);
  or ACTIVE_ADDRESS_ERROR (ACTIVE_ADDRESS_OUT_OF_RANGE, ACTIVE_OFFSET_ADDRESS_ERROR_out, ACTIVE_ADDRESS_RANGE_GATE_out);
endmodule

module OrArithmeticCircuit (
  input  OR_ACTIVATED,
  input  [15:0] LEFT,
  input  [15:0] RIGHT,
  input  INPUT_VALID,
  output [15:0] RESULT,
  output RESULT_VALID
);

  wire [15:0] BITWISE_OR_out;

  assign BITWISE_OR_out = LEFT | RIGHT;  // OR_Gate BITWISE_OR, 16 bits wide
  Multiplexer #(.width(16)) multiplexer_1 (.in0({16{1'b0}}), .in1(BITWISE_OR_out), .out(RESULT), .sel(OR_ACTIVATED));
  and ACTIVE_OR_VALID (RESULT_VALID, OR_ACTIVATED, INPUT_VALID);

  // Notes on the sheet:
  //   bitwise OR: inactive outputs are neutral
endmodule

module XorArithmeticCircuit (
  input  XOR_ACTIVATED,
  input  [15:0] LEFT,
  input  [15:0] RIGHT,
  input  INPUT_VALID,
  output [15:0] RESULT,
  output RESULT_VALID
);

  wire [15:0] BITWISE_XOR_out;

  assign BITWISE_XOR_out = LEFT ^ RIGHT;  // XOR_Gate BITWISE_XOR, 16 bits wide
  Multiplexer #(.width(16)) multiplexer_1 (.in0({16{1'b0}}), .in1(BITWISE_XOR_out), .out(RESULT), .sel(XOR_ACTIVATED));
  and ACTIVE_XOR_VALID (RESULT_VALID, XOR_ACTIVATED, INPUT_VALID);

  // Notes on the sheet:
  //   bitwise XOR: inactive outputs are neutral
endmodule

module JumpBox (
  input  ERROR_OVF,
  input  ERROR_DIV0,
  input  ERROR_ADDR,
  input  ERROR_INV,
  input  ERROR_ILL,
  input  ERROR_INPUT,
  input  JUMP_ADR,
  input  JUMP_ZERO,
  input  JUMP_NOT_ZERO,
  input  JUMP_NEGATIVE,
  input  JUMP_ERROR,
  input  JUMP_NOT_ERROR,
  input  NEGATIVE,
  input  ZERO,
  output IS_NOT_ZERO,
  output DEC_JUMP_NOT_ZERO
);

  wire ANY_ERROR_FOR_JUMP_out, INVERT_ANY_ERROR_FOR_JUMP_NOT_ERROR_out, INVERT_ZERO_FOR_JZ_out,
       JUMP_ADR_OR_JNZ_CONTROL_out, JUMP_ADR_OR_NOT_ZERO_out, JUMP_ERROR_AND_ANY_ERROR_out,
       JUMP_ERROR_OR_PREVIOUS_CONTROLS_out, JUMP_ERROR_OR_PREVIOUS_TAKEN_out, JUMP_NEGATIVE_AND_NEGATIVE_out,
       JUMP_NEGATIVE_OR_PREVIOUS_CONTROLS_out, JUMP_NEGATIVE_OR_PREVIOUS_TAKEN_out,
       JUMP_NOT_ERROR_AND_NO_ERROR_out, JUMP_ZERO_AND_ZERO_out, JUMP_ZERO_OR_PREVIOUS_CONTROLS_out,
       JUMP_ZERO_OR_PREVIOUS_TAKEN_out;

  or ANY_ERROR_FOR_JUMP (ANY_ERROR_FOR_JUMP_out, ERROR_OVF, ERROR_DIV0, ERROR_ADDR, ERROR_INV, ERROR_ILL, ERROR_INPUT);
  or JUMP_ADR_OR_JNZ_CONTROL (JUMP_ADR_OR_JNZ_CONTROL_out, JUMP_NOT_ZERO, JUMP_ADR);
  not INVERT_ZERO_FOR_JZ (INVERT_ZERO_FOR_JZ_out, ZERO);
  or JUMP_ZERO_OR_PREVIOUS_CONTROLS (JUMP_ZERO_OR_PREVIOUS_CONTROLS_out, JUMP_ADR_OR_JNZ_CONTROL_out, JUMP_ZERO);
  or JUMP_ADR_OR_NOT_ZERO (JUMP_ADR_OR_NOT_ZERO_out, JUMP_ADR, ZERO);
  and JUMP_ZERO_AND_ZERO (JUMP_ZERO_AND_ZERO_out, JUMP_ZERO, INVERT_ZERO_FOR_JZ_out);
  and JUMP_NEGATIVE_AND_NEGATIVE (JUMP_NEGATIVE_AND_NEGATIVE_out, JUMP_NEGATIVE, NEGATIVE);
  or JUMP_NEGATIVE_OR_PREVIOUS_CONTROLS (JUMP_NEGATIVE_OR_PREVIOUS_CONTROLS_out, JUMP_ZERO_OR_PREVIOUS_CONTROLS_out, JUMP_NEGATIVE);
  or JUMP_ZERO_OR_PREVIOUS_TAKEN (JUMP_ZERO_OR_PREVIOUS_TAKEN_out, JUMP_ADR_OR_NOT_ZERO_out, JUMP_ZERO_AND_ZERO_out);
  or JUMP_NEGATIVE_OR_PREVIOUS_TAKEN (JUMP_NEGATIVE_OR_PREVIOUS_TAKEN_out, JUMP_ZERO_OR_PREVIOUS_TAKEN_out, JUMP_NEGATIVE_AND_NEGATIVE_out);
  and JUMP_ERROR_AND_ANY_ERROR (JUMP_ERROR_AND_ANY_ERROR_out, JUMP_NOT_ERROR, ANY_ERROR_FOR_JUMP_out);
  not INVERT_ANY_ERROR_FOR_JUMP_NOT_ERROR (INVERT_ANY_ERROR_FOR_JUMP_NOT_ERROR_out, ANY_ERROR_FOR_JUMP_out);
  or JUMP_ERROR_OR_PREVIOUS_CONTROLS (JUMP_ERROR_OR_PREVIOUS_CONTROLS_out, JUMP_NOT_ERROR, JUMP_NEGATIVE_OR_PREVIOUS_CONTROLS_out);
  or JUMP_ERROR_OR_PREVIOUS_TAKEN (JUMP_ERROR_OR_PREVIOUS_TAKEN_out, JUMP_NEGATIVE_OR_PREVIOUS_TAKEN_out, JUMP_ERROR_AND_ANY_ERROR_out);
  and JUMP_NOT_ERROR_AND_NO_ERROR (JUMP_NOT_ERROR_AND_NO_ERROR_out, JUMP_ERROR, INVERT_ANY_ERROR_FOR_JUMP_NOT_ERROR_out);
  or JUMP_NOT_ERROR_OR_PREVIOUS_CONTROLS (IS_NOT_ZERO, JUMP_ERROR_OR_PREVIOUS_CONTROLS_out, JUMP_ERROR);
  or JUMP_NOT_ERROR_OR_PREVIOUS_TAKEN (DEC_JUMP_NOT_ZERO, JUMP_ERROR_OR_PREVIOUS_TAKEN_out, JUMP_NOT_ERROR_AND_NO_ERROR_out);
endmodule
