// Logisim project TinyCPU_Operator.circ as structural Verilog: 1 circuit, main circuit TinyCPUOperator
module TinyCPUOperator (
  input  RESET,
  input  STEP,
  input  RUN,
  output CPU_CLOCK,
  output [15:0] PRINT_VALUE,
  output [15:0] RAW_MEMORY_VALUE,
  output RAW_MEMORY_VALID,
  output [15:0] PRINT_ADDRESS_VALUE,
  output PRINT_ADDRESS_VALID,
  output [15:0] EXTERNAL_WRITE_VALUE,
  output EXTERNAL_WRITE_VALID,
  output EXTERNAL_WRITE_ENABLE,
  output INSTRUCTION_BOUNDARY,
  output ENABLE_INTERRUPTS_REQUEST,
  output DISABLE_INTERRUPTS_REQUEST,
  output RETURN_FROM_INTERRUPT_REQUEST,
  output ERROR_OVF,
  output ERROR_DIV0,
  output ERROR_ADDR,
  output ERROR_INV,
  output ERROR_ILL,
  output ERROR_INPUT,
  output [11:0] NEXT_PC,
  output [15:0] ADDRESS,
  output PRINT_ENABLE,
  output PRINT_ADDRESS_ENABLE,
  output HALTED,
  output HALTED_WITH_ERROR
);

  wire RUN_CLOCK_ENABLED_out, RUN_CLOCK_out;

  Clock RUN_CLOCK (.out(RUN_CLOCK_out));
  and RUN_CLOCK_ENABLED (RUN_CLOCK_ENABLED_out, RUN, RUN_CLOCK_out);
  or CPU_CLOCK_SOURCE (CPU_CLOCK, STEP, RUN_CLOCK_ENABLED_out);
  // TinyCPUMain tinycpumain_1: pin names not known; wires that end beside it: CPU_CLOCK, RESET, 1'b1, 1'b1, 12'h1, 16'h1, 1'b1, 1'b1, 1'b1, PRINT_VALUE, RAW_MEMORY_VALUE, RAW_MEMORY_VALID, PRINT_ADDRESS_VALUE, PRINT_ADDRESS_VALID, EXTERNAL_WRITE_VALUE, EXTERNAL_WRITE_VALID, EXTERNAL_WRITE_ENABLE, INSTRUCTION_BOUNDARY, ENABLE_INTERRUPTS_REQUEST, DISABLE_INTERRUPTS_REQUEST, RETURN_FROM_INTERRUPT_REQUEST, ERROR_OVF, ERROR_DIV0, ERROR_ADDR, ERROR_INV, ERROR_ILL, ERROR_INPUT, NEXT_PC, ADDRESS, PRINT_ENABLE, PRINT_ADDRESS_ENABLE, HALTED

  // Notes on the sheet:
  //   TinyCPU Operator Panel — RESET, STEP or RUN; 0/1 are logic levels, U is unknown, E is an electrical error
  //   Countdown demo: reset, release RESET, then STEP until PRINT_ENABLE; normal and error halt are separate indicators.
  //   CPU state (hex buses; boolean status bits)
  //   HALTED = normal halt
  //   Errors: OVF / DIV0 / ADDR / INV / ILL / INPUT
  //   HALTED_WITH_ERROR = regular error halt
endmodule
