// Logisim project TinyCPU-FetchDecodeControls.circ as structural Verilog: 1 circuit, main circuit FetchDecodeControls
module FetchDecodeControls (
  input  [5:0] OPCODE,
  output ADD_OPERAND,
  output SUB_OPERAND,
  output MUL_OPERAND,
  output DIV_OPERAND,
  output AND_OPERAND,
  output OR_OPERAND,
  output XOR_OPERAND,
  output CONST_ARGUMENT,
  output ADDR_ARGUMENT,
  output ADDR_REG_ARGUMENT,
  output ADDR_REG_OFFS_ARGUMENT,
  output NOT,
  output JUMP_ADR,
  output JUMP_ZERO,
  output JUMP_NOT_ZERO,
  output JUMP_NEGATIVE,
  output JUMP_ERROR,
  output JUMP_NOT_ERROR,
  output LOAD_CONST,
  output LOAD_ADR,
  output LOAD_ADR_REG,
  output LOAD_REG_OFF,
  output LD_REG_CONST,
  output LD_REG_ADR,
  output STORE_ADR,
  output STORE_ADR_REG,
  output STORE_REG_OFF,
  output SET_OVF,
  output SET_DIV0,
  output SET_ADDR,
  output SET_INV,
  output SET_ILL,
  output SET_INPUT,
  output CLEAR_ERROR,
  output INPUT,
  output PRINT,
  output PRINT_ADR,
  output HALT,
  output HALT_ERROR,
  output INVALID_OPERAND
);

  wire decoder_1_out0, decoder_1_out1, decoder_1_out2, decoder_1_out3, decoder_1_out4, decoder_1_out5,
       decoder_1_out6, decoder_1_out7, decoder_1_out8, decoder_1_out9, decoder_1_out10, decoder_1_out11,
       decoder_1_out12, decoder_1_out13, decoder_1_out14, decoder_1_out15, decoder_1_out16, decoder_1_out17,
       decoder_1_out18, decoder_1_out19, decoder_1_out20, decoder_1_out21, decoder_1_out22, decoder_1_out23,
       decoder_1_out24, decoder_1_out25, decoder_1_out26, decoder_1_out27, decoder_1_out56, decoder_1_out57,
       decoder_1_out58, decoder_1_out59, decoder_1_out60, decoder_1_out61, decoder_1_out62, decoder_1_out63;

  Decoder #(.select(6)) decoder_1 (
    .out0(decoder_1_out0), .out1(decoder_1_out1), .out2(decoder_1_out2), .out3(decoder_1_out3),
    .out4(decoder_1_out4), .out5(decoder_1_out5), .out6(decoder_1_out6), .out7(decoder_1_out7),
    .out8(decoder_1_out8), .out9(decoder_1_out9), .out10(decoder_1_out10), .out11(decoder_1_out11),
    .out12(decoder_1_out12), .out13(decoder_1_out13), .out14(decoder_1_out14), .out15(decoder_1_out15),
    .out16(decoder_1_out16), .out17(decoder_1_out17), .out18(decoder_1_out18), .out19(decoder_1_out19),
    .out20(decoder_1_out20), .out21(decoder_1_out21), .out22(decoder_1_out22), .out23(decoder_1_out23),
    .out24(decoder_1_out24), .out25(decoder_1_out25), .out26(decoder_1_out26), .out27(decoder_1_out27),
    .out28(NOT), .out29(JUMP_ADR), .out30(JUMP_ZERO), .out31(JUMP_NOT_ZERO), .out32(JUMP_NEGATIVE),
    .out33(JUMP_ERROR), .out34(JUMP_NOT_ERROR), .out35(LOAD_CONST), .out36(LOAD_ADR), .out37(LOAD_ADR_REG),
    .out38(LOAD_REG_OFF), .out39(LD_REG_CONST), .out40(LD_REG_ADR), .out41(STORE_ADR), .out42(STORE_ADR_REG),
    .out43(STORE_REG_OFF), .out44(SET_OVF), .out45(SET_DIV0), .out46(SET_ADDR), .out47(SET_INV),
    .out48(SET_ILL), .out49(SET_INPUT), .out50(CLEAR_ERROR), .out51(INPUT), .out52(PRINT), .out53(PRINT_ADR),
    .out54(HALT), .out55(HALT_ERROR), .out56(decoder_1_out56), .out57(decoder_1_out57),
    .out58(decoder_1_out58), .out59(decoder_1_out59), .out60(decoder_1_out60), .out61(decoder_1_out61),
    .out62(decoder_1_out62), .out63(decoder_1_out63), .sel(OPCODE));  // open: en
  or ADD_OPERAND_SELECT (ADD_OPERAND, decoder_1_out0, decoder_1_out1, decoder_1_out2, decoder_1_out3);
  or SUB_OPERAND_SELECT (SUB_OPERAND, decoder_1_out4, decoder_1_out5, decoder_1_out6, decoder_1_out7);
  or MUL_OPERAND_SELECT (MUL_OPERAND, decoder_1_out8, decoder_1_out9, decoder_1_out10, decoder_1_out11);
  or DIV_OPERAND_SELECT (DIV_OPERAND, decoder_1_out12, decoder_1_out13, decoder_1_out14, decoder_1_out15);
  or AND_OPERAND_SELECT (AND_OPERAND, decoder_1_out16, decoder_1_out17, decoder_1_out18, decoder_1_out19);
  or OR_OPERAND_SELECT (OR_OPERAND, decoder_1_out20, decoder_1_out21, decoder_1_out22, decoder_1_out23);
  or XOR_OPERAND_SELECT (XOR_OPERAND, decoder_1_out24, decoder_1_out25, decoder_1_out26, decoder_1_out27);
  or CONST_ARGUMENT_SELECT (CONST_ARGUMENT, decoder_1_out0, decoder_1_out4, decoder_1_out8, decoder_1_out12, decoder_1_out16, decoder_1_out20, decoder_1_out24);
  or ADDR_ARGUMENT_SELECT (ADDR_ARGUMENT, decoder_1_out1, decoder_1_out5, decoder_1_out9, decoder_1_out13, decoder_1_out17, decoder_1_out21, decoder_1_out25);
  or ADDR_REG_ARGUMENT_SELECT (ADDR_REG_ARGUMENT, decoder_1_out2, decoder_1_out6, decoder_1_out10, decoder_1_out14, decoder_1_out18, decoder_1_out22, decoder_1_out26);
  or ADDR_REG_OFFS_ARGUMENT_SELECT (ADDR_REG_OFFS_ARGUMENT, decoder_1_out3, decoder_1_out7, decoder_1_out11, decoder_1_out15, decoder_1_out19, decoder_1_out23, decoder_1_out27);
  or INVALID_OPERAND_SELECT (INVALID_OPERAND, decoder_1_out56, decoder_1_out57, decoder_1_out58, decoder_1_out59, decoder_1_out60, decoder_1_out61, decoder_1_out62, decoder_1_out63);

  // Notes on the sheet:
  //   ADD_OPERAND: addiert den gewählten Operanden
  //   SUB_OPERAND: subtrahiert den gewählten Operanden
  //   MUL_OPERAND: multipliziert mit dem gewählten Operanden
  //   DIV_OPERAND: dividiert durch den gewählten Operanden
  //   AND_OPERAND: bitweises UND mit dem gewählten Operanden
  //   OR_OPERAND: bitweises ODER mit dem gewählten Operanden
  //   XOR_OPERAND: bitweises XOR mit dem gewählten Operanden
  //   CONST_ARGUMENT: verwendet die Konstante als Argument
  //   ADDR_ARGUMENT: verwendet den Speicherwert an der Adresse
  //   ADDR_REG_ARGUMENT: verwendet den Speicherwert am Adressregister
  //   ADDR_REG_OFFS_ARGUMENT: verwendet den Speicherwert bei Adressregister plus Offset
  //   NOT: invertiert den Akkumulator bitweise
  //   JUMP_ADR: springt unbedingt zur Adresse
  //   JUMP_ZERO: springt, wenn der Akkumulator null ist
  //   JUMP_NOT_ZERO: springt, wenn der Akkumulator nicht null ist
  //   JUMP_NEGATIVE: springt, wenn der Akkumulator negativ ist
  //   JUMP_ERROR: springt, wenn ein Fehler gesetzt ist
  //   JUMP_NOT_ERROR: springt, wenn kein Fehler gesetzt ist
  //   LOAD_CONST: lädt die Konstante in den Akkumulator
  //   LOAD_ADR: lädt den Speicherwert an der Adresse
  //   LOAD_ADR_REG: lädt den Speicherwert am Adressregister
  //   LOAD_REG_OFF: lädt den Speicherwert bei Adressregister plus Offset
  //   LD_REG_CONST: lädt die Konstante in das Adressregister
  //   LD_REG_ADR: lädt das Adressregister aus der Speicheradresse
  //   STORE_ADR: speichert den Akkumulator an der Adresse
  //   STORE_ADR_REG: speichert den Akkumulator am Adressregister
  //   STORE_REG_OFF: speichert den Akkumulator bei Adressregister plus Offset
  //   SET_OVF: setzt den Überlauffehler
  //   SET_DIV0: setzt den Fehler Division durch null
  //   SET_ADDR: setzt den Adressfehler
  //   SET_INV: setzt den Ungültigkeitsfehler
  //   SET_ILL: setzt den Fehler für unbekannte Befehle
  //   SET_INPUT: setzt den Eingabefehler
  //   CLEAR_ERROR: löscht alle Fehlermerker
  //   INPUT: liest einen Wert in den Akkumulator
  //   PRINT: gibt den Akkumulator aus
  //   PRINT_ADR: gibt den Speicherwert an der Adresse aus
  //   HALT: hält die CPU regulär an
  //   HALT_ERROR: hält die CPU mit Fehler an
  //   INVALID_OPERAND: meldet einen reservierten Opcode als ungültig
endmodule
